// Logisim project Controller Device--CdM8 conection.circ as structural Verilog: 1 circuit, main circuit main
module main (
  input  [7:0] in_1,
  input  block,
  input  [7:0] in_3,
  input  [7:0] in_4,
  output [7:0] out_5
);

  wire and_1_out, and_2_out, and_3_out, and_4_out, cdm_8_mark5_1_p1, cdm_8_mark5_1_p2, cdm_8_mark5_1_p4,
       cdm_8_mark5_1_p5, cdm_8_mark5_1_p6, clock, code, comparator_1_eq, comparator_2_eq, comparator_3_eq,
       comparator_4_eq, data, I_Osel, in_out_prime, mem, nand_1_out, not_1_out, not_2_out, not_3_out,
       not_4_out, RAM;
  wire [3:0] I_Oadr;
  wire [7:0] cdm_8_mark5_1_p10, cdm_8_mark5_1_p11, I_Odat, register_2_q;
  wire [7:4] cdm_8_mark5_1_p9;

  Comparator #(.width(4), .mode("unsigned")) comparator_1 (
    .a(I_Oadr), .b(4'b0011), .eq(comparator_1_eq));  // open: gt, lt
  Comparator #(.width(4), .mode("unsigned")) comparator_2 (
    .a(I_Oadr), .b(4'b1000), .eq(comparator_2_eq));  // open: gt, lt
  and and_1 (and_1_out, I_Osel, comparator_1_eq);
  and and_2 (and_2_out, I_Osel, comparator_2_eq);
  Comparator #(.width(4), .mode("unsigned")) comparator_3 (
    .a(I_Oadr), .b(4'b0101), .eq(comparator_3_eq));  // open: gt, lt
  and and_3 (and_3_out, I_Osel, comparator_4_eq);
  Comparator #(.width(4), .mode("unsigned")) comparator_4 (
    .a(I_Oadr), .b(4'b0100), .eq(comparator_4_eq));  // open: gt, lt
  and and_4 (and_4_out, I_Osel, comparator_3_eq);
  assign I_Odat = and_1_out ? register_2_q : 8'bz;  // Controlled_Buffer controlled_buffer_1
  assign I_Odat = and_3_out ? in_3 : 8'bz;  // Controlled_Buffer controlled_buffer_2
  assign I_Odat = and_4_out ? in_4 : 8'bz;  // Controlled_Buffer controlled_buffer_3
  Register register_1 (.D(I_Odat), .en(not_1_out), .Q(out_5), .clk(and_2_out));  // open: clr
  not not_1 (not_1_out, block);
  not not_2 (not_2_out, block);
  Register register_2 (.D(in_1), .en(not_2_out), .Q(register_2_q), .clk(clock), .clr(block));
  // Probe on I_Oadr
  // Probe on I_Odat
  // Probe on cdm_8_mark5_1_p5
  // Probe on cdm_8_mark5_1_p4
  // Probe on cdm_8_mark5_1_p2
  // Probe on cdm_8_mark5_1_p1
  Clock clock_1 (.out(clock));
  and and_5 (I_Osel, not_3_out, clock, data);
  // Probe on nothing
  // Probe on nothing
  not not_3 (not_3_out, nand_1_out);
  and and_6 (RAM, nand_1_out, data);
  // CdM_8_mark5 cdm_8_mark5_1: pin names not known; wires that end beside it: cdm_8_mark5_1_p1, cdm_8_mark5_1_p2, clock, cdm_8_mark5_1_p4, cdm_8_mark5_1_p5, cdm_8_mark5_1_p6, mem, in_out_prime, {cdm_8_mark5_1_p9, I_Oadr}, cdm_8_mark5_1_p10, cdm_8_mark5_1_p11
  nand nand_1 (nand_1_out, cdm_8_mark5_1_p9[4], cdm_8_mark5_1_p9[5], cdm_8_mark5_1_p9[6], cdm_8_mark5_1_p9[7]);
  Decoder #(.disabled(0)) decoder_1 (.out0(code), .out1(data), .sel(cdm_8_mark5_1_p6), .en(mem));
  assign I_Odat = not_4_out ? cdm_8_mark5_1_p10 : 8'bz;  // Controlled_Buffer controlled_buffer_4
  not not_4 (not_4_out, in_out_prime);
  assign cdm_8_mark5_1_p11 = in_out_prime ? I_Odat : 8'bz;  // Controlled_Buffer controlled_buffer_5
  Pull_Resistor pull_resistor_1 (.node(I_Oadr[0]));
  Pull_Resistor pull_resistor_2 (.node(I_Oadr[1]));
  Pull_Resistor pull_resistor_3 (.node(I_Oadr[2]));
  Pull_Resistor pull_resistor_4 (.node(I_Oadr[3]));
  Pull_Resistor pull_resistor_5 (.node(cdm_8_mark5_1_p9[4]));
  Pull_Resistor pull_resistor_6 (.node(cdm_8_mark5_1_p9[5]));
  Pull_Resistor pull_resistor_7 (.node(cdm_8_mark5_1_p9[6]));
  Pull_Resistor pull_resistor_8 (.node(cdm_8_mark5_1_p9[7]));
  ROM rom_1 (.addr({cdm_8_mark5_1_p9, I_Oadr}), .data(I_Odat), .sel(code));
  RAM ram_1 (.addr({cdm_8_mark5_1_p9, I_Oadr}), .data(I_Odat), .sel(RAM), .clk(clock), .ld(in_out_prime));  // open: clr

  // Other names for the same wires on the sheet: blogckyuyuyjhjy = block; rd_wr_prime = in_out_prime

  // Notes on the sheet:
  //   INPUT Vxy (0b00yyyxxx)
  //   INPUT BallX 8b
  //   INPUT BallY 8b
  //   OUTPUT 0xf8-0xff addr
  //   RightBat Y
  //   *to controller
  //   I/O BUS
  //   4 lower bit adr
  //   "RIGHT_BAT_PREDICTOR***.asm"
  //   INSTR
  //   contents of rom_1 (hex, n*v repeats v):
  //   d0 f3 b0 d2 f5 ba 0 e1 e d0 f8 a2 ee 0 d3 4 43 f ed 19 d0 f8 a2 ee 0 d1 f4 b5 85 d3 e0 1d 91 d3 7f
  //   4d d3 20 73 ea 64 98 98 98 d3 3 73 e1 40 c2 6 d0 0 d3 0 95 23 d0 0 19 23 c6 ee 4f d3 2 73 e1 4d d3 0
  //   d0 0 95 23 ee 4f d3 0 d0 0 16 23 d0 1 43 f e1 5b ee 5d 86 8e d0 f8 a2 ee 0 ee b2 98 98 98 d3 f8 5c
  //   84 d3 4 73 e1 7c d3 0 d0 0 95 23 d0 0 95 23 ee 9f d3 3 73 e1 90 c2 6 d3 0 d0 0 95 23 d0 0 19 23 c6
  //   ee 9f d3 2 73 e1 9d d3 0 d0 0 95 23 ee 9f d3 0 d0 0 16 23 d0 1 43 f ed ad 86 8e ee ad d0 f8 a2 ee 0
  //   d4
  //   DATA
endmodule
