// Logisim project tennis.circ as structural Verilog
module main (
);

  wire [3:0] joystick_1_y;
  wire [4:0] display_1_out_2, display_2_out_2, display_3_out_2;

  _7_Segment_Display u_7_segment_display_1 ();  // open: g, f, a, b, e, d, c, dp
  Joystick joystick_1 (.y(joystick_1_y));  // open: x
  Kinematic_controller kinematic_controller_1 ();
  _7_Segment_Display u_7_segment_display_2 ();  // open: g, f, a, b, e, d, c, dp
  // NOT_Gate not_1 has open pins: in=joystick_1_y, out=open
  DotMatrix #(.matrixcols(32), .matrixrows(32)) dotmatrix_1 ();  // open: col0, col1, col2, col3, col4, col5, col6, col7, col8, col9, col10, col11, col12, col13, col14, col15, col16, col17, col18, col19, col20, col21, col22, col23, col24, col25, col26, col27, col28, col29, col30, col31
  display display_1 (.out_2(display_1_out_2));  // open: in_1, out_3, out_4, out_5, out_6
  display display_2 (.in_1(display_1_out_2), .out_2(display_2_out_2));  // open: out_3, out_4, out_5, out_6
  display display_3 (.in_1(display_2_out_2), .out_2(display_3_out_2));  // open: out_3, out_4, out_5, out_6
  display display_4 (.in_1(display_3_out_2));  // open: out_2, out_3, out_4, out_5, out_6
  _7_Segment_Display u_7_segment_display_3 ();  // open: g, f, a, b, e, d, c, dp
  _7_Segment_Display u_7_segment_display_4 ();  // open: g, f, a, b, e, d, c, dp
endmodule

module display (
  input  [4:0] in_1,
  output [4:0] out_2,
  output [4:0] out_3,
  output [4:0] out_4,
  output [4:0] out_5,
  output [4:0] out_6
);

  wire bit_extender_1_out;
  wire [4:0] subtractor_1_out, undriven;

  Adder #(.width(5)) adder_1 (.a(5'b00001), .b(in_1), .out(out_2));  // open: cin, cout
  ballX ballx_1 (.in_1(out_3));
  ballY bally_1 (.in_1(undriven));
  Subtractor #(.width(5)) subtractor_1 (.a(out_2), .b(out_3), .out(subtractor_1_out));  // open: bin, bout
  leftBatY leftbaty_1 (.in_1(out_5));
  rightBatY rightbaty_1 (.in_1(out_6));
  Multiplexer #(.width(5), .enable("false")) multiplexer_1 (
    .in0(undriven), .out(out_4), .sel(bit_extender_1_out));  // open: in1
  Bit_Extender #(.in_width(5), .out_width(1)) bit_extender_1 (.in(subtractor_1_out), .out(bit_extender_1_out));
endmodule

module ballX (
  input  [4:0] in_1
);
endmodule

module ballY (
  input  [4:0] in_1
);
endmodule

module leftBatY (
  input  [4:0] in_1
);
endmodule

module rightBatY (
  input  [4:0] in_1
);
endmodule
