// Logisim project tennis_123.circ as structural Verilog: 4 circuits, main circuit main
module main (
  input  [4:0] in_1,
  input  [4:0] in_2,
  input  [4:0] in_3,
  input  [4:0] in_4
);

  wire [3:0] joystick_1_y;
  wire [4:0] videosub_1_ballx, videosub_1_bally, videosub_1_chipid, videosub_1_leftbat, videosub_1_rightbat,
       videosub_2_ballx, videosub_2_bally, videosub_2_chipid, videosub_2_leftbat, videosub_2_rightbat,
       videosub_3_ballx, videosub_3_bally, videosub_3_chipid, videosub_3_leftbat, videosub_3_rightbat;
  wire [31:0] videosub_1_out_6, videosub_1_out_7, videosub_1_out_8, videosub_1_out_9, videosub_1_out_10,
       videosub_1_out_11, videosub_1_out_12, videosub_1_out_13, videosub_2_out_6, videosub_2_out_7,
       videosub_2_out_8, videosub_2_out_9, videosub_2_out_10, videosub_2_out_11, videosub_2_out_12,
       videosub_2_out_13, videosub_3_out_6, videosub_3_out_7, videosub_3_out_8, videosub_3_out_9,
       videosub_3_out_10, videosub_3_out_11, videosub_3_out_12, videosub_3_out_13, videosub_4_out_6,
       videosub_4_out_7, videosub_4_out_8, videosub_4_out_9, videosub_4_out_10, videosub_4_out_11,
       videosub_4_out_12, videosub_4_out_13;

  Kinematic_controller kinematic_controller_1 ();  // open: BallX, BallY, RightBat, Vxy, reset
  _7_Segment_Display u_7_segment_display_1 ();  // open: g, f, a, b, e, d, c, dp
  Joystick joystick_1 (.y(joystick_1_y));  // open: x
  _7_Segment_Display u_7_segment_display_2 ();  // open: g, f, a, b, e, d, c, dp
  // NOT_Gate not_1 has open pins: in=joystick_1_y, out=open
  videoSub videosub_1 (
    .out_6(videosub_1_out_6), .out_7(videosub_1_out_7), .out_8(videosub_1_out_8), .out_9(videosub_1_out_9),
    .out_10(videosub_1_out_10), .out_11(videosub_1_out_11), .out_12(videosub_1_out_12),
    .out_13(videosub_1_out_13), .in_1(in_1), .in_2(in_2), .in_3(in_3), .in_4(in_4), .in_5({5{1'b0}}),
    .BallX(videosub_1_ballx), .BallY(videosub_1_bally), .rightBat(videosub_1_rightbat),
    .leftBat(videosub_1_leftbat), .chipID(videosub_1_chipid));
  DotMatrix #(.matrixcols(32), .matrixrows(32)) dotmatrix_1 (
    .col0(videosub_1_out_6), .col1(videosub_1_out_7), .col2(videosub_1_out_8), .col3(videosub_1_out_9),
    .col4(videosub_1_out_10), .col5(videosub_1_out_11), .col6(videosub_1_out_12), .col7(videosub_1_out_13),
    .col8(videosub_2_out_6), .col9(videosub_2_out_7), .col10(videosub_2_out_8), .col11(videosub_2_out_9),
    .col12(videosub_2_out_10), .col13(videosub_2_out_11), .col14(videosub_2_out_12),
    .col15(videosub_2_out_13), .col16(videosub_3_out_6), .col17(videosub_3_out_7), .col18(videosub_3_out_8),
    .col19(videosub_3_out_9), .col20(videosub_3_out_10), .col21(videosub_3_out_11),
    .col22(videosub_3_out_12), .col23(videosub_3_out_13), .col24(videosub_4_out_6), .col25(videosub_4_out_7),
    .col26(videosub_4_out_8), .col27(videosub_4_out_9), .col28(videosub_4_out_10), .col29(videosub_4_out_11),
    .col30(videosub_4_out_12), .col31(videosub_4_out_13));
  videoSub videosub_2 (
    .out_6(videosub_2_out_6), .out_7(videosub_2_out_7), .out_8(videosub_2_out_8), .out_9(videosub_2_out_9),
    .out_10(videosub_2_out_10), .out_11(videosub_2_out_11), .out_12(videosub_2_out_12),
    .out_13(videosub_2_out_13), .in_1(videosub_1_ballx), .in_2(videosub_1_bally), .in_3(videosub_1_rightbat),
    .in_4(videosub_1_leftbat), .in_5(videosub_1_chipid), .BallX(videosub_2_ballx), .BallY(videosub_2_bally),
    .rightBat(videosub_2_rightbat), .leftBat(videosub_2_leftbat), .chipID(videosub_2_chipid));
  videoSub videosub_3 (
    .out_6(videosub_3_out_6), .out_7(videosub_3_out_7), .out_8(videosub_3_out_8), .out_9(videosub_3_out_9),
    .out_10(videosub_3_out_10), .out_11(videosub_3_out_11), .out_12(videosub_3_out_12),
    .out_13(videosub_3_out_13), .in_1(videosub_2_ballx), .in_2(videosub_2_bally), .in_3(videosub_2_rightbat),
    .in_4(videosub_2_leftbat), .in_5(videosub_2_chipid), .BallX(videosub_3_ballx), .BallY(videosub_3_bally),
    .rightBat(videosub_3_rightbat), .leftBat(videosub_3_leftbat), .chipID(videosub_3_chipid));
  videoSub videosub_4 (
    .out_6(videosub_4_out_6), .out_7(videosub_4_out_7), .out_8(videosub_4_out_8), .out_9(videosub_4_out_9),
    .out_10(videosub_4_out_10), .out_11(videosub_4_out_11), .out_12(videosub_4_out_12),
    .out_13(videosub_4_out_13), .in_1(videosub_3_ballx), .in_2(videosub_3_bally), .in_3(videosub_3_rightbat),
    .in_4(videosub_3_leftbat), .in_5(videosub_3_chipid));  // open: BallX, BallY, rightBat, leftBat, chipID
  _7_Segment_Display u_7_segment_display_3 ();  // open: g, f, a, b, e, d, c, dp
  _7_Segment_Display u_7_segment_display_4 ();  // open: g, f, a, b, e, d, c, dp
endmodule

module videochip (
  input  [4:0] BallX,
  input  [4:0] BallY,
  input  [4:0] rightBat,
  input  [4:0] leftBat,
  input  [4:0] chipID,
  output [31:0] out_6,
  output [4:0] BallX_2,
  output [4:0] BallY_2,
  output [4:0] rightBat_2,
  output [4:0] leftBat_2,
  output [4:0] chipID_2
);

  wire comparator_1_eq, comparator_2_eq, comparator_3_eq;
  wire [31:0] decoder_1_out0, decoder_2_out0, decoder_3_out0, multiplexer_1_out, multiplexer_2_out,
       multiplexer_3_out, or_1_out, or_2_out, shifter_1_out, shifter_2_out, shifter_3_out, shifter_4_out;

  Adder #(.width(5)) adder_1 (.a(chipID), .b(5'b00001), .out(chipID_2));  // open: cin, cout
  Comparator #(.width(5), .mode("unsigned")) comparator_1 (
    .a(BallX), .b(chipID), .eq(comparator_1_eq));  // open: gt, lt
  Comparator #(.width(5), .mode("unsigned")) comparator_2 (
    .a(chipID), .b(5'b00011), .eq(comparator_2_eq));  // open: gt, lt
  Comparator #(.width(5), .mode("unsigned")) comparator_3 (
    .a(chipID), .b(5'b11100), .eq(comparator_3_eq));  // open: gt, lt
  Decoder #(.select(5), .enable("false")) decoder_1 (
    .out0(decoder_1_out0[0]), .out1(decoder_1_out0[1]), .out2(decoder_1_out0[2]), .out3(decoder_1_out0[3]),
    .out4(decoder_1_out0[4]), .out5(decoder_1_out0[5]), .out6(decoder_1_out0[6]), .out7(decoder_1_out0[7]),
    .out8(decoder_1_out0[8]), .out9(decoder_1_out0[9]), .out10(decoder_1_out0[10]),
    .out11(decoder_1_out0[11]), .out12(decoder_1_out0[12]), .out13(decoder_1_out0[13]),
    .out14(decoder_1_out0[14]), .out15(decoder_1_out0[15]), .out16(decoder_1_out0[16]),
    .out17(decoder_1_out0[17]), .out18(decoder_1_out0[18]), .out19(decoder_1_out0[19]),
    .out20(decoder_1_out0[20]), .out21(decoder_1_out0[21]), .out22(decoder_1_out0[22]),
    .out23(decoder_1_out0[23]), .out24(decoder_1_out0[24]), .out25(decoder_1_out0[25]),
    .out26(decoder_1_out0[26]), .out27(decoder_1_out0[27]), .out28(decoder_1_out0[28]),
    .out29(decoder_1_out0[29]), .out30(decoder_1_out0[30]), .out31(decoder_1_out0[31]), .sel(rightBat));
  Decoder #(.select(5), .enable("false")) decoder_2 (
    .out0(decoder_2_out0[0]), .out1(decoder_2_out0[1]), .out2(decoder_2_out0[2]), .out3(decoder_2_out0[3]),
    .out4(decoder_2_out0[4]), .out5(decoder_2_out0[5]), .out6(decoder_2_out0[6]), .out7(decoder_2_out0[7]),
    .out8(decoder_2_out0[8]), .out9(decoder_2_out0[9]), .out10(decoder_2_out0[10]),
    .out11(decoder_2_out0[11]), .out12(decoder_2_out0[12]), .out13(decoder_2_out0[13]),
    .out14(decoder_2_out0[14]), .out15(decoder_2_out0[15]), .out16(decoder_2_out0[16]),
    .out17(decoder_2_out0[17]), .out18(decoder_2_out0[18]), .out19(decoder_2_out0[19]),
    .out20(decoder_2_out0[20]), .out21(decoder_2_out0[21]), .out22(decoder_2_out0[22]),
    .out23(decoder_2_out0[23]), .out24(decoder_2_out0[24]), .out25(decoder_2_out0[25]),
    .out26(decoder_2_out0[26]), .out27(decoder_2_out0[27]), .out28(decoder_2_out0[28]),
    .out29(decoder_2_out0[29]), .out30(decoder_2_out0[30]), .out31(decoder_2_out0[31]), .sel(BallY));
  Decoder #(.select(5), .enable("false")) decoder_3 (
    .out0(decoder_3_out0[0]), .out1(decoder_3_out0[1]), .out2(decoder_3_out0[2]), .out3(decoder_3_out0[3]),
    .out4(decoder_3_out0[4]), .out5(decoder_3_out0[5]), .out6(decoder_3_out0[6]), .out7(decoder_3_out0[7]),
    .out8(decoder_3_out0[8]), .out9(decoder_3_out0[9]), .out10(decoder_3_out0[10]),
    .out11(decoder_3_out0[11]), .out12(decoder_3_out0[12]), .out13(decoder_3_out0[13]),
    .out14(decoder_3_out0[14]), .out15(decoder_3_out0[15]), .out16(decoder_3_out0[16]),
    .out17(decoder_3_out0[17]), .out18(decoder_3_out0[18]), .out19(decoder_3_out0[19]),
    .out20(decoder_3_out0[20]), .out21(decoder_3_out0[21]), .out22(decoder_3_out0[22]),
    .out23(decoder_3_out0[23]), .out24(decoder_3_out0[24]), .out25(decoder_3_out0[25]),
    .out26(decoder_3_out0[26]), .out27(decoder_3_out0[27]), .out28(decoder_3_out0[28]),
    .out29(decoder_3_out0[29]), .out30(decoder_3_out0[30]), .out31(decoder_3_out0[31]), .sel(leftBat));
  Multiplexer #(.width(32), .enable("false")) multiplexer_1 (
    .in0({32{1'b0}}), .in1(decoder_2_out0), .out(multiplexer_1_out), .sel(comparator_1_eq));
  Multiplexer #(.width(32), .enable("false")) multiplexer_2 (
    .in0({32{1'b0}}), .in1(decoder_3_out0), .out(multiplexer_2_out), .sel(comparator_2_eq));
  Multiplexer #(.width(32), .enable("false")) multiplexer_3 (
    .in0({32{1'b0}}), .in1(decoder_1_out0), .out(multiplexer_3_out), .sel(comparator_3_eq));
  Shifter #(.width(32)) shifter_1 (.in(multiplexer_2_out), .\dist (5'b00001), .out(shifter_1_out));
  Shifter #(.width(32)) shifter_2 (.in(multiplexer_3_out), .\dist (5'b00001), .out(shifter_2_out));
  Shifter #(.width(32)) shifter_3 (.in(shifter_1_out), .\dist (5'b00001), .out(shifter_3_out));
  Shifter #(.width(32)) shifter_4 (.in(shifter_2_out), .\dist (5'b00001), .out(shifter_4_out));
  assign or_1_out = multiplexer_2_out | shifter_1_out | shifter_3_out;  // OR_Gate or_1, 32 bits wide
  assign or_2_out = multiplexer_3_out | shifter_2_out | shifter_4_out;  // OR_Gate or_2, 32 bits wide
  assign out_6 = multiplexer_1_out | or_1_out | or_2_out;  // OR_Gate or_3, 32 bits wide

  assign BallX_2 = BallX;
  assign BallY_2 = BallY;
  assign leftBat_2 = leftBat;
  assign rightBat_2 = rightBat;
endmodule

module Kinematic_controller (
  input  [4:0] BallX,
  input  [4:0] BallY,
  input  [7:0] Vxy,
  input  [4:0] RightBat,
  input  reset
);

  wire clock_1_out, comparator_1_lt, comparator_2_eq, comparator_2_lt, comparator_3_lt,
       controlled_buffer_1_out;
  wire [2:0] adder_3_out, controlled_buffer_2_out, controlled_buffer_3_out, register_1_q, register_2_q,
       register_3_q;
  wire [4:0] adder_1_out, or_1_out, undriven, undriven_2, undriven_3;
  wire [7:0] bit_extender_1_out, counter_1_q;

  Counter counter_1 (.Q(counter_1_q), .clk(controlled_buffer_1_out), .clr(reset));  // open: load, D, count, carry
  assign controlled_buffer_1_out = comparator_1_lt ? clock_1_out : 1'bz;  // Controlled_Buffer controlled_buffer_1
  Clock clock_1 (.out(clock_1_out));
  assign controlled_buffer_2_out = comparator_1_lt ? Vxy[2:0] : 3'bz;  // Controlled_Buffer controlled_buffer_2
  assign controlled_buffer_3_out = comparator_1_lt ? Vxy[5:3] : 3'bz;  // Controlled_Buffer controlled_buffer_3
  Comparator #(.mode("unsigned")) comparator_1 (.a(counter_1_q), .b(8'h2), .lt(comparator_1_lt));  // open: gt, eq
  assign or_1_out = BallX | BallY;  // OR_Gate or_1, 5 bits wide
  assign bit_extender_1_out = {{3{1'b0}}, or_1_out};  // Bit_Extender bit_extender_1
  Register #(.width(3)) register_1 (
    .D(controlled_buffer_2_out), .Q(register_1_q), .clk(clock_1_out), .clr(reset));  // open: en
  Register #(.width(3)) register_2 (
    .D(controlled_buffer_3_out), .Q(register_2_q), .clk(clock_1_out), .clr(reset));  // open: en
  Register #(.width(3)) register_3 (.D(bit_extender_1_out[2:0]), .Q(register_3_q));  // open: en, clk, clr
  Register #(.width(3)) register_4 (.D(bit_extender_1_out[5:3]));  // open: en, Q, clk, clr
  Adder #(.width(5)) adder_1 (.a(undriven), .b(undriven_3), .out(adder_1_out));  // open: cin, cout
  Comparator #(.width(3)) comparator_2 (
    .a(bit_extender_1_out[2:0]), .b(3'b100), .eq(comparator_2_eq), .lt(comparator_2_lt));  // open: gt
  Adder #(.width(5)) adder_2 (.a(undriven_2), .b(BallY));  // open: out, cin, cout
  Adder #(.width(3)) adder_3 (
    .a(bit_extender_1_out[2:0]), .b(3'b001), .out(adder_3_out), .cin(comparator_2_lt));  // open: cout
  Comparator #(.width(5)) comparator_3 (.a(BallX), .b(5'b10000), .lt(comparator_3_lt));  // open: gt, eq
  // also tied to GND on the sheet: {bit_extender_1_out[6], bit_extender_1_out[7]}

  // Notes on the sheet:
  //   3bitY
  //   3bitX
  //   Vx chngs(after reflecting the ball)
  //   Vy 
endmodule

module videoSub (
  input  [4:0] in_1,
  input  [4:0] in_2,
  input  [4:0] in_3,
  input  [4:0] in_4,
  input  [4:0] in_5,
  output [31:0] out_6,
  output [31:0] out_7,
  output [31:0] out_8,
  output [31:0] out_9,
  output [31:0] out_10,
  output [31:0] out_11,
  output [31:0] out_12,
  output [31:0] out_13,
  output [4:0] BallX,
  output [4:0] BallY,
  output [4:0] rightBat,
  output [4:0] leftBat,
  output [4:0] chipID
);

  wire [4:0] videochip_1_ballx_2, videochip_1_bally_2, videochip_1_chipid_2, videochip_1_leftbat_2,
       videochip_1_rightbat_2, videochip_2_ballx_2, videochip_2_bally_2, videochip_2_chipid_2,
       videochip_2_leftbat_2, videochip_2_rightbat_2, videochip_3_ballx_2, videochip_3_bally_2,
       videochip_3_chipid_2, videochip_3_leftbat_2, videochip_3_rightbat_2, videochip_4_ballx_2,
       videochip_4_bally_2, videochip_4_chipid_2, videochip_4_leftbat_2, videochip_4_rightbat_2,
       videochip_5_ballx_2, videochip_5_bally_2, videochip_5_chipid_2, videochip_5_leftbat_2,
       videochip_5_rightbat_2, videochip_6_ballx_2, videochip_6_bally_2, videochip_6_chipid_2,
       videochip_6_leftbat_2, videochip_6_rightbat_2, videochip_7_ballx_2, videochip_7_bally_2,
       videochip_7_chipid_2, videochip_7_leftbat_2, videochip_7_rightbat_2;

  videochip videochip_1 (
    .chipID(in_5), .leftBat(in_4), .rightBat(in_3), .BallY(in_2), .BallX(in_1),
    .BallX_2(videochip_1_ballx_2), .BallY_2(videochip_1_bally_2), .rightBat_2(videochip_1_rightbat_2),
    .leftBat_2(videochip_1_leftbat_2), .chipID_2(videochip_1_chipid_2), .out_6(out_6));
  videochip videochip_2 (
    .chipID(videochip_1_chipid_2), .leftBat(videochip_1_leftbat_2), .rightBat(videochip_1_rightbat_2),
    .BallY(videochip_1_bally_2), .BallX(videochip_1_ballx_2), .BallX_2(videochip_2_ballx_2),
    .BallY_2(videochip_2_bally_2), .rightBat_2(videochip_2_rightbat_2), .leftBat_2(videochip_2_leftbat_2),
    .chipID_2(videochip_2_chipid_2), .out_6(out_7));
  videochip videochip_3 (
    .chipID(videochip_2_chipid_2), .leftBat(videochip_2_leftbat_2), .rightBat(videochip_2_rightbat_2),
    .BallY(videochip_2_bally_2), .BallX(videochip_2_ballx_2), .BallX_2(videochip_3_ballx_2),
    .BallY_2(videochip_3_bally_2), .rightBat_2(videochip_3_rightbat_2), .leftBat_2(videochip_3_leftbat_2),
    .chipID_2(videochip_3_chipid_2), .out_6(out_8));
  videochip videochip_4 (
    .chipID(videochip_3_chipid_2), .leftBat(videochip_3_leftbat_2), .rightBat(videochip_3_rightbat_2),
    .BallY(videochip_3_bally_2), .BallX(videochip_3_ballx_2), .BallX_2(videochip_4_ballx_2),
    .BallY_2(videochip_4_bally_2), .rightBat_2(videochip_4_rightbat_2), .leftBat_2(videochip_4_leftbat_2),
    .chipID_2(videochip_4_chipid_2), .out_6(out_9));
  videochip videochip_5 (
    .chipID(videochip_4_chipid_2), .leftBat(videochip_4_leftbat_2), .rightBat(videochip_4_rightbat_2),
    .BallY(videochip_4_bally_2), .BallX(videochip_4_ballx_2), .BallX_2(videochip_5_ballx_2),
    .BallY_2(videochip_5_bally_2), .rightBat_2(videochip_5_rightbat_2), .leftBat_2(videochip_5_leftbat_2),
    .chipID_2(videochip_5_chipid_2), .out_6(out_10));
  videochip videochip_6 (
    .chipID(videochip_5_chipid_2), .leftBat(videochip_5_leftbat_2), .rightBat(videochip_5_rightbat_2),
    .BallY(videochip_5_bally_2), .BallX(videochip_5_ballx_2), .BallX_2(videochip_6_ballx_2),
    .BallY_2(videochip_6_bally_2), .rightBat_2(videochip_6_rightbat_2), .leftBat_2(videochip_6_leftbat_2),
    .chipID_2(videochip_6_chipid_2), .out_6(out_11));
  videochip videochip_7 (
    .chipID(videochip_6_chipid_2), .leftBat(videochip_6_leftbat_2), .rightBat(videochip_6_rightbat_2),
    .BallY(videochip_6_bally_2), .BallX(videochip_6_ballx_2), .BallX_2(videochip_7_ballx_2),
    .BallY_2(videochip_7_bally_2), .rightBat_2(videochip_7_rightbat_2), .leftBat_2(videochip_7_leftbat_2),
    .chipID_2(videochip_7_chipid_2), .out_6(out_12));
  videochip videochip_8 (
    .chipID(videochip_7_chipid_2), .leftBat(videochip_7_leftbat_2), .rightBat(videochip_7_rightbat_2),
    .BallY(videochip_7_bally_2), .BallX(videochip_7_ballx_2), .BallX_2(BallX), .BallY_2(BallY),
    .rightBat_2(rightBat), .leftBat_2(leftBat), .chipID_2(chipID), .out_6(out_13));
endmodule
