// Logisim project tennis_cdmtest.circ as structural Verilog: 9 circuits, main circuit main
module main (
  input  [7:0] in_1,
  input  [7:0] in_2,
  input  [2:0] vx,
  input  [2:0] vy
);

  wire clock_1_out, RES_out;
  wire [3:0] P_0, P_1, R_0, R_1;
  wire [4:0] joystick, joystick_1_y, kinematic_controller_1_ballx_2, kinematic_controller_1_bally_2, robot,
       videosub_1_ballx, videosub_1_bally, videosub_1_chipid, videosub_1_leftbat, videosub_1_rightbat,
       videosub_2_ballx, videosub_2_bally, videosub_2_chipid, videosub_2_leftbat, videosub_2_rightbat,
       videosub_3_ballx, videosub_3_bally, videosub_3_chipid, videosub_3_leftbat, videosub_3_rightbat;
  wire [31:0] videosub_1_out_6, videosub_1_out_7, videosub_1_out_8, videosub_1_out_9, videosub_1_out_10,
       videosub_1_out_11, videosub_1_out_12, videosub_1_out_13, videosub_2_out_6, videosub_2_out_7,
       videosub_2_out_8, videosub_2_out_9, videosub_2_out_10, videosub_2_out_11, videosub_2_out_12,
       videosub_2_out_13, videosub_3_out_6, videosub_3_out_7, videosub_3_out_8, videosub_3_out_9,
       videosub_3_out_10, videosub_3_out_11, videosub_3_out_12, videosub_3_out_13, videosub_4_out_6,
       videosub_4_out_7, videosub_4_out_8, videosub_4_out_9, videosub_4_out_10, videosub_4_out_11,
       videosub_4_out_12, videosub_4_out_13;

  Joystick #(.bits(5)) joystick_1 (.y(joystick_1_y));  // open: x
  // Probe on in_1
  // Probe on in_2
  assign joystick = ~joystick_1_y;  // NOT_Gate not_1, 5 bits wide
  Kinematic_controller kinematic_controller_1 (
    .BallX(in_1), .BallY(in_2), .Vx(vx), .reset(RES_out), .BallX_2(kinematic_controller_1_ballx_2),
    .BallY_2(kinematic_controller_1_bally_2), .clock(clock_1_out), .out_10(robot), .out_8(R_1), .out_9(R_0),
    .LeftBat(joystick), .out_11(P_1), .out_12(P_0), .Vx_2(vy));
  Button RES (.out(RES_out));
  Clock clock_1 (.out(clock_1_out));
  Hex_Digit_Display hex_digit_display_1 (.value(P_1));  // open: dp
  Hex_Digit_Display hex_digit_display_2 (.value(P_0));  // open: dp
  DotMatrix #(.matrixcols(32), .matrixrows(32)) dotmatrix_1 (
    .col0(videosub_1_out_6), .col1(videosub_1_out_7), .col2(videosub_1_out_8), .col3(videosub_1_out_9),
    .col4(videosub_1_out_10), .col5(videosub_1_out_11), .col6(videosub_1_out_12), .col7(videosub_1_out_13),
    .col8(videosub_2_out_6), .col9(videosub_2_out_7), .col10(videosub_2_out_8), .col11(videosub_2_out_9),
    .col12(videosub_2_out_10), .col13(videosub_2_out_11), .col14(videosub_2_out_12),
    .col15(videosub_2_out_13), .col16(videosub_3_out_6), .col17(videosub_3_out_7), .col18(videosub_3_out_8),
    .col19(videosub_3_out_9), .col20(videosub_3_out_10), .col21(videosub_3_out_11),
    .col22(videosub_3_out_12), .col23(videosub_3_out_13), .col24(videosub_4_out_6), .col25(videosub_4_out_7),
    .col26(videosub_4_out_8), .col27(videosub_4_out_9), .col28(videosub_4_out_10), .col29(videosub_4_out_11),
    .col30(videosub_4_out_12), .col31(videosub_4_out_13));
  videoSub videosub_1 (
    .out_6(videosub_1_out_6), .out_7(videosub_1_out_7), .out_8(videosub_1_out_8), .out_9(videosub_1_out_9),
    .out_10(videosub_1_out_10), .out_11(videosub_1_out_11), .out_12(videosub_1_out_12),
    .out_13(videosub_1_out_13), .in_1(kinematic_controller_1_ballx_2), .in_2(kinematic_controller_1_bally_2),
    .in_3(robot), .in_4(joystick), .in_5({5{1'b0}}), .BallX(videosub_1_ballx), .BallY(videosub_1_bally),
    .rightBat(videosub_1_rightbat), .leftBat(videosub_1_leftbat), .chipID(videosub_1_chipid));
  // Probe on robot
  videoSub videosub_2 (
    .out_6(videosub_2_out_6), .out_7(videosub_2_out_7), .out_8(videosub_2_out_8), .out_9(videosub_2_out_9),
    .out_10(videosub_2_out_10), .out_11(videosub_2_out_11), .out_12(videosub_2_out_12),
    .out_13(videosub_2_out_13), .in_1(videosub_1_ballx), .in_2(videosub_1_bally), .in_3(videosub_1_rightbat),
    .in_4(videosub_1_leftbat), .in_5(videosub_1_chipid), .BallX(videosub_2_ballx), .BallY(videosub_2_bally),
    .rightBat(videosub_2_rightbat), .leftBat(videosub_2_leftbat), .chipID(videosub_2_chipid));
  videoSub videosub_3 (
    .out_6(videosub_3_out_6), .out_7(videosub_3_out_7), .out_8(videosub_3_out_8), .out_9(videosub_3_out_9),
    .out_10(videosub_3_out_10), .out_11(videosub_3_out_11), .out_12(videosub_3_out_12),
    .out_13(videosub_3_out_13), .in_1(videosub_2_ballx), .in_2(videosub_2_bally), .in_3(videosub_2_rightbat),
    .in_4(videosub_2_leftbat), .in_5(videosub_2_chipid), .BallX(videosub_3_ballx), .BallY(videosub_3_bally),
    .rightBat(videosub_3_rightbat), .leftBat(videosub_3_leftbat), .chipID(videosub_3_chipid));
  videoSub videosub_4 (
    .out_6(videosub_4_out_6), .out_7(videosub_4_out_7), .out_8(videosub_4_out_8), .out_9(videosub_4_out_9),
    .out_10(videosub_4_out_10), .out_11(videosub_4_out_11), .out_12(videosub_4_out_12),
    .out_13(videosub_4_out_13), .in_1(videosub_3_ballx), .in_2(videosub_3_bally), .in_3(videosub_3_rightbat),
    .in_4(videosub_3_leftbat), .in_5(videosub_3_chipid));  // open: BallX, BallY, rightBat, leftBat, chipID
  Hex_Digit_Display hex_digit_display_3 (.value(R_1));  // open: dp
  Hex_Digit_Display hex_digit_display_4 (.value(R_0));  // open: dp

  // Other names for the same wires on the sheet: X[7:0] = in_1; Y[7:0] = in_2
endmodule

module videochip (
  input  [4:0] BallX,
  input  [4:0] BallY,
  input  [4:0] rightBat,
  input  [4:0] leftBat,
  input  [4:0] chipID,
  output [31:0] out_6,
  output [4:0] BallX_2,
  output [4:0] BallY_2,
  output [4:0] rightBat_2,
  output [4:0] leftBat_2,
  output [4:0] chipID_2
);

  wire comparator_1_eq, comparator_2_eq, comparator_3_eq;
  wire [31:0] decoder_1_out0, decoder_2_out0, decoder_3_out0, multiplexer_1_out, multiplexer_2_out,
       multiplexer_3_out, or_1_out, or_2_out, shifter_1_out, shifter_2_out, shifter_3_out, shifter_4_out;

  Adder #(.width(5)) adder_1 (.a(chipID), .b(5'b00001), .out(chipID_2));  // open: cin, cout
  Comparator #(.width(5), .mode("unsigned")) comparator_1 (
    .a(BallX), .b(chipID), .eq(comparator_1_eq));  // open: gt, lt
  Comparator #(.width(5), .mode("unsigned")) comparator_2 (
    .a(chipID), .b(5'b00011), .eq(comparator_2_eq));  // open: gt, lt
  Comparator #(.width(5), .mode("unsigned")) comparator_3 (
    .a(chipID), .b(5'b11100), .eq(comparator_3_eq));  // open: gt, lt
  // Probe on 5'b11100
  Decoder #(.select(5), .enable("false")) decoder_1 (
    .out0(decoder_1_out0[0]), .out1(decoder_1_out0[1]), .out2(decoder_1_out0[2]), .out3(decoder_1_out0[3]),
    .out4(decoder_1_out0[4]), .out5(decoder_1_out0[5]), .out6(decoder_1_out0[6]), .out7(decoder_1_out0[7]),
    .out8(decoder_1_out0[8]), .out9(decoder_1_out0[9]), .out10(decoder_1_out0[10]),
    .out11(decoder_1_out0[11]), .out12(decoder_1_out0[12]), .out13(decoder_1_out0[13]),
    .out14(decoder_1_out0[14]), .out15(decoder_1_out0[15]), .out16(decoder_1_out0[16]),
    .out17(decoder_1_out0[17]), .out18(decoder_1_out0[18]), .out19(decoder_1_out0[19]),
    .out20(decoder_1_out0[20]), .out21(decoder_1_out0[21]), .out22(decoder_1_out0[22]),
    .out23(decoder_1_out0[23]), .out24(decoder_1_out0[24]), .out25(decoder_1_out0[25]),
    .out26(decoder_1_out0[26]), .out27(decoder_1_out0[27]), .out28(decoder_1_out0[28]),
    .out29(decoder_1_out0[29]), .out30(decoder_1_out0[30]), .out31(decoder_1_out0[31]), .sel(rightBat));
  Decoder #(.select(5), .enable("false")) decoder_2 (
    .out0(decoder_2_out0[0]), .out1(decoder_2_out0[1]), .out2(decoder_2_out0[2]), .out3(decoder_2_out0[3]),
    .out4(decoder_2_out0[4]), .out5(decoder_2_out0[5]), .out6(decoder_2_out0[6]), .out7(decoder_2_out0[7]),
    .out8(decoder_2_out0[8]), .out9(decoder_2_out0[9]), .out10(decoder_2_out0[10]),
    .out11(decoder_2_out0[11]), .out12(decoder_2_out0[12]), .out13(decoder_2_out0[13]),
    .out14(decoder_2_out0[14]), .out15(decoder_2_out0[15]), .out16(decoder_2_out0[16]),
    .out17(decoder_2_out0[17]), .out18(decoder_2_out0[18]), .out19(decoder_2_out0[19]),
    .out20(decoder_2_out0[20]), .out21(decoder_2_out0[21]), .out22(decoder_2_out0[22]),
    .out23(decoder_2_out0[23]), .out24(decoder_2_out0[24]), .out25(decoder_2_out0[25]),
    .out26(decoder_2_out0[26]), .out27(decoder_2_out0[27]), .out28(decoder_2_out0[28]),
    .out29(decoder_2_out0[29]), .out30(decoder_2_out0[30]), .out31(decoder_2_out0[31]), .sel(BallY));
  Decoder #(.select(5), .enable("false")) decoder_3 (
    .out0(decoder_3_out0[0]), .out1(decoder_3_out0[1]), .out2(decoder_3_out0[2]), .out3(decoder_3_out0[3]),
    .out4(decoder_3_out0[4]), .out5(decoder_3_out0[5]), .out6(decoder_3_out0[6]), .out7(decoder_3_out0[7]),
    .out8(decoder_3_out0[8]), .out9(decoder_3_out0[9]), .out10(decoder_3_out0[10]),
    .out11(decoder_3_out0[11]), .out12(decoder_3_out0[12]), .out13(decoder_3_out0[13]),
    .out14(decoder_3_out0[14]), .out15(decoder_3_out0[15]), .out16(decoder_3_out0[16]),
    .out17(decoder_3_out0[17]), .out18(decoder_3_out0[18]), .out19(decoder_3_out0[19]),
    .out20(decoder_3_out0[20]), .out21(decoder_3_out0[21]), .out22(decoder_3_out0[22]),
    .out23(decoder_3_out0[23]), .out24(decoder_3_out0[24]), .out25(decoder_3_out0[25]),
    .out26(decoder_3_out0[26]), .out27(decoder_3_out0[27]), .out28(decoder_3_out0[28]),
    .out29(decoder_3_out0[29]), .out30(decoder_3_out0[30]), .out31(decoder_3_out0[31]), .sel(leftBat));
  Multiplexer #(.width(32), .enable("false")) multiplexer_1 (
    .in0({32{1'b0}}), .in1(decoder_2_out0), .out(multiplexer_1_out), .sel(comparator_1_eq));
  Multiplexer #(.width(32), .enable("false")) multiplexer_2 (
    .in0({32{1'b0}}), .in1(decoder_3_out0), .out(multiplexer_2_out), .sel(comparator_2_eq));
  Multiplexer #(.width(32), .enable("false")) multiplexer_3 (
    .in0({32{1'b0}}), .in1(decoder_1_out0), .out(multiplexer_3_out), .sel(comparator_3_eq));
  Shifter #(.width(32)) shifter_1 (.in(multiplexer_2_out), .\dist (5'b00001), .out(shifter_1_out));
  Shifter #(.width(32)) shifter_2 (.in(multiplexer_3_out), .\dist (5'b00001), .out(shifter_2_out));
  Shifter #(.width(32)) shifter_3 (.in(shifter_1_out), .\dist (5'b00001), .out(shifter_3_out));
  Shifter #(.width(32)) shifter_4 (.in(shifter_2_out), .\dist (5'b00001), .out(shifter_4_out));
  assign or_1_out = multiplexer_2_out | shifter_1_out | shifter_3_out;  // OR_Gate or_1, 32 bits wide
  assign or_2_out = multiplexer_3_out | shifter_2_out | shifter_4_out;  // OR_Gate or_2, 32 bits wide
  assign out_6 = multiplexer_1_out | or_1_out | or_2_out;  // OR_Gate or_3, 32 bits wide

  assign BallX_2 = BallX;
  assign BallY_2 = BallY;
  assign leftBat_2 = leftBat;
  assign rightBat_2 = rightBat;
endmodule

module Kinematic_controller (
  input  [7:0] BallX,
  input  [7:0] BallY,
  input  [2:0] Vx,
  input  [2:0] Vx_2,
  input  reset,
  input  clock,
  input  [4:0] LeftBat,
  output [3:0] out_8,
  output [3:0] out_9,
  output [4:0] out_10,
  output [3:0] out_11,
  output [3:0] out_12,
  output [4:0] BallX_2,
  output [4:0] BallY_2
);

  wire and_1_out, and_2_out, and_5_out, and_6_out, and_7_out, and_8_out, and_9_out, and_10_out, C_left_flag,
       C_right_flag, clock_t, comparator_3_lt, comparator_6_gt, comparator_7_eq, comparator_8_eq,
       comparator_9_eq, comparator_10_eq, controlled_buffer_1_out, counter_3_q, is_hit_the_left_1_out_3,
       is_hit_the_left_2_out_3, left_reflect, multiplexer_1_out, multiplexer_2_out, multiplexer_4_out,
       multiplexer_5_out, NO_NAGIB, not_2_out, not_3_out, not_4_out, not_5_out, not_6_out, not_7_out,
       not_8_out, not_9_out, not_10_out, not_11_out, not_12_out, not_13_out, not_14_out, not_15_out,
       not_16_out, not_17_out, not_18_out, nrun_prime, or_1_out, or_2_out, P_0_reset, R_0_reset, reflect,
       reflect_t, reflectX, right_reflect, run, stop_P, stop_R, X_C_flag, Y_C_flag;
  wire [2:0] controlled_buffer_4_out, controlled_buffer_5_out;
  wire [5:0] VXYTOROB;
  wire [7:0] adder_1_out, adder_2_out, adder_3_out, adder_5_out, BallX_POST_sum, BallX_PRE_SUM,
       BallY_POST_sum, BallY_PRE_SUM, controlled_buffer_6_out, controlled_buffer_7_out,
       controlled_buffer_11_out, controlled_buffer_12_out, counter_1_q, invert_v_1_out_2, invert_v_2_out_2,
       main_1_out_5, player_score_update, robot_score_update, shifter_1_out, shifter_2_out, shifter_3_out,
       Vx_POST, Vx_PRE, Vy_POST, Vy_PRE;
  wire [7:4] counter_4_q, counter_5_q;

  Counter counter_1 (.Q(counter_1_q), .clk(controlled_buffer_1_out), .clr(reset));  // open: load, D, count, carry
  assign controlled_buffer_1_out = run ? clock_t : 1'bz;  // Controlled_Buffer controlled_buffer_1
  Controller_Device__CdM8_conection_main main_1 (
    .in_1({2'b00, VXYTOROB}), .out_5(main_1_out_5), .block(NO_NAGIB), .in_3(BallX_PRE_SUM),
    .in_4(BallY_PRE_SUM));
  Comparator #(.mode("unsigned")) comparator_1 (.a(counter_1_q), .b(8'h2), .lt(run));  // open: gt, eq
  Counter #(.width(1), .max('h1)) counter_2 (.Q(clock_t), .clk(counter_3_q));  // open: load, D, count, carry, clr
  Counter #(.width(1), .max('h1)) counter_3 (.Q(counter_3_q), .clk(clock));  // open: load, D, count, carry, clr
  assign BallX_POST_sum = run ? BallX : 8'bz;  // Controlled_Buffer controlled_buffer_2
  assign BallY_POST_sum = run ? BallY : 8'bz;  // Controlled_Buffer controlled_buffer_3
  assign controlled_buffer_4_out = run ? Vx : 3'bz;  // Controlled_Buffer controlled_buffer_4
  _3_bit_to_8_sign u_3_bit_to_8_sign_1 (.in_1(controlled_buffer_4_out), .out_2(Vx_POST));
  _3_bit_to_8_sign u_3_bit_to_8_sign_2 (.in_1(controlled_buffer_5_out), .out_2(Vy_POST));
  assign controlled_buffer_5_out = run ? Vx_2 : 3'bz;  // Controlled_Buffer controlled_buffer_5
  not not_1 (nrun_prime, run);
  Multiplexer multiplexer_1 (.in0(1'b0), .in1(1'b1), .out(multiplexer_1_out), .sel(Y_C_flag));  // open: en
  Multiplexer multiplexer_2 (.in0(1'b1), .in1(1'b0), .out(multiplexer_2_out), .sel(Y_C_flag));  // open: en
  Register register_1 (.D(Vx_POST), .Q(Vx_PRE), .clk(clock_t), .clr(reset));  // open: en
  Register register_2 (.D(Vy_POST), .Q(Vy_PRE), .clk(clock_t), .clr(reset));  // open: en
  Multiplexer multiplexer_3 (
    .in0(multiplexer_1_out), .in1(multiplexer_2_out), .out(reflect), .sel(Vy_PRE[7]));  // open: en
  Shifter #(.shift("lr")) shifter_1 (.in(main_1_out_5), .\dist (3'b011), .out(shifter_1_out));
  Register register_3 (.D(BallX_POST_sum), .en(not_2_out), .Q(BallX_PRE_SUM), .clk(clock_t), .clr(reset));
  not not_2 (not_2_out, reflectX);
  Register register_4 (.D(BallY_POST_sum), .en(not_3_out), .Q(BallY_PRE_SUM), .clk(clock_t), .clr(reset));
  not not_3 (not_3_out, reflect);
  assign controlled_buffer_6_out = nrun_prime ? Vy_PRE : 8'bz;  // Controlled_Buffer controlled_buffer_6
  invert_V invert_v_1 (.in_1(Vy_PRE), .out_2(invert_v_1_out_2));
  Bit_Extender #(.out_width(5)) bit_extender_1 (.in(shifter_1_out), .out(out_10));
  Comparator #(.mode("unsigned")) comparator_2 (.a(BallX_PRE_SUM), .b(8'h7f), .gt(NO_NAGIB));  // open: eq, lt
  assign controlled_buffer_7_out = not_4_out ? controlled_buffer_6_out : 8'bz;  // Controlled_Buffer controlled_buffer_7
  not not_4 (not_4_out, reflect);
  and and_1 (and_1_out, reflect, not_5_out);
  not not_5 (not_5_out, clock_t);
  Multiplexer multiplexer_4 (.in0(1'b0), .in1(1'b1), .out(multiplexer_4_out), .sel(X_C_flag));  // open: en
  Multiplexer multiplexer_5 (.in0(1'b1), .in1(1'b0), .out(multiplexer_5_out), .sel(X_C_flag));  // open: en
  Adder adder_1 (.a(Vx_PRE), .b(BallX_PRE_SUM), .out(adder_1_out), .cout(X_C_flag));  // open: cin
  Adder adder_2 (.a(BallY_PRE_SUM), .b(Vy_PRE), .out(adder_2_out), .cout(Y_C_flag));  // open: cin
  assign Vy_POST = nrun_prime ? controlled_buffer_7_out : 8'bz;  // Controlled_Buffer controlled_buffer_8
  Multiplexer #(.width(8), .enable("false")) multiplexer_6 (
    .in0(Vy_PRE), .in1(invert_v_1_out_2), .out(controlled_buffer_7_out), .sel(and_1_out));
  Multiplexer multiplexer_7 (
    .in0(multiplexer_4_out), .in1(multiplexer_5_out), .out(reflect_t), .sel(Vx_PRE[7]));  // open: en
  Shifter #(.shift("lr")) shifter_2 (.in(BallX_PRE_SUM), .\dist (3'b011), .out(shifter_2_out));
  Shifter #(.shift("lr")) shifter_3 (.in(BallY_PRE_SUM), .\dist (3'b011), .out(shifter_3_out));
  assign BallX_POST_sum = nrun_prime ? adder_1_out : 8'bz;  // Controlled_Buffer controlled_buffer_9
  assign BallY_POST_sum = nrun_prime ? adder_2_out : 8'bz;  // Controlled_Buffer controlled_buffer_10
  Bit_Extender #(.out_width(5)) bit_extender_2 (.in(shifter_2_out), .out(BallX_2));
  Bit_Extender #(.out_width(5)) bit_extender_3 (.in(shifter_3_out), .out(BallY_2));
  assign controlled_buffer_11_out = nrun_prime ? Vx_PRE : 8'bz;  // Controlled_Buffer controlled_buffer_11
  _8_to_3 u_8_to_3_1 (.in_1(Vx_POST), .out_2(VXYTOROB[2:0]));
  _8_to_3 u_8_to_3_2 (.in_1(Vy_POST), .out_2(VXYTOROB[5:3]));
  assign controlled_buffer_12_out = not_6_out ? controlled_buffer_11_out : 8'bz;  // Controlled_Buffer controlled_buffer_12
  not not_6 (not_6_out, reflectX);
  invert_V invert_v_2 (.in_1(Vx_PRE), .out_2(invert_v_2_out_2));
  not not_7 (not_7_out, left_reflect);
  and and_2 (and_2_out, not_7_out, not_8_out, not_9_out);
  not not_8 (not_8_out, reflect_t);
  not not_9 (not_9_out, right_reflect);
  assign Vx_POST = nrun_prime ? controlled_buffer_12_out : 8'bz;  // Controlled_Buffer controlled_buffer_13
  Multiplexer #(.width(8), .enable("false")) multiplexer_8 (
    .in0(Vx_PRE), .in1(invert_v_2_out_2), .out(controlled_buffer_12_out), .sel(reflectX));
  not not_10 (not_10_out, and_2_out);
  not not_11 (not_11_out, clock_t);
  Comparator #(.mode("unsigned")) comparator_3 (.a(BallX_POST_sum), .b(8'h15), .lt(comparator_3_lt));  // open: gt, eq
  and and_3 (reflectX, not_10_out, not_11_out);
  Adder adder_3 (.a(BallX_PRE_SUM), .b(8'he4), .out(adder_3_out));  // open: cin, cout
  not not_12 (not_12_out, C_left_flag);
  is_hit_the_left is_hit_the_left_1 (.in_1(BallY_PRE_SUM), .leftBat(LeftBat), .out_3(is_hit_the_left_1_out_3));
  Comparator #(.width(4), .mode("unsigned")) comparator_4 (
    .a(robot_score_update[3:0]), .b(4'b1010), .eq(R_0_reset));  // open: gt, lt
  Comparator #(.width(4), .mode("unsigned")) comparator_5 (
    .a(player_score_update[3:0]), .b(4'b1010), .eq(P_0_reset));  // open: gt, lt
  Comparator #(.mode("unsigned")) comparator_6 (.a(BallX_POST_sum), .b(8'he9), .gt(comparator_6_gt));  // open: eq, lt
  Adder adder_4 (.a(Vx_PRE), .b(adder_3_out), .cout(C_left_flag));  // open: out, cin
  and and_4 (left_reflect, not_12_out, is_hit_the_left_1_out_3, Vx_PRE[7]);
  Counter #(.max('h9)) counter_4 (
    .Q({counter_4_q, out_8}), .clk(and_5_out), .clr(reset));  // open: load, D, count, carry
  and and_5 (and_5_out, R_0_reset, not_16_out);
  Counter #(.max('h9)) counter_5 (
    .Q({counter_5_q, out_11}), .clk(and_6_out), .clr(reset));  // open: load, D, count, carry
  and and_6 (and_6_out, P_0_reset, not_17_out);
  not not_13 (not_13_out, X_C_flag);
  not not_14 (not_14_out, stop_R);
  and and_7 (and_7_out, comparator_7_eq, comparator_8_eq);
  Comparator #(.width(4), .mode("unsigned")) comparator_7 (
    .a(robot_score_update[3:0]), .b(4'b1001), .eq(comparator_7_eq));  // open: gt, lt
  Comparator #(.mode("unsigned")) comparator_8 (
    .a({counter_4_q, out_8}), .b(8'h9), .eq(comparator_8_eq));  // open: gt, lt
  not not_15 (not_15_out, stop_P);
  and and_8 (and_8_out, comparator_9_eq, comparator_10_eq);
  Comparator #(.width(4), .mode("unsigned")) comparator_9 (
    .a(player_score_update[3:0]), .b(4'b1001), .eq(comparator_9_eq));  // open: gt, lt
  Comparator #(.mode("unsigned")) comparator_10 (
    .a({counter_5_q, out_11}), .b(8'h9), .eq(comparator_10_eq));  // open: gt, lt
  Counter #(.max('ha), .ongoal("load")) counter_6 (
    .D({8{1'b0}}), .Q(robot_score_update), .clk(and_9_out), .clr(or_1_out));  // open: load, count, carry
  and and_9 (and_9_out, reflect_t, comparator_3_lt, not_13_out);
  Counter #(.max('ha), .ongoal("load")) counter_7 (
    .D({8{1'b0}}), .Q(player_score_update), .clk(and_10_out), .clr(or_2_out));  // open: load, count, carry
  and and_10 (and_10_out, X_C_flag, comparator_6_gt, reflect_t);
  Register #(.width(4)) register_5 (
    .D(robot_score_update[3:0]), .en(not_14_out), .Q(out_9), .clk(clock_t), .clr(reset));
  Counter #(.width(1), .max('h1), .ongoal("stay")) counter_8 (
    .Q(stop_R), .clk(and_7_out), .clr(reset));  // open: load, D, count, carry
  not not_16 (not_16_out, comparator_8_eq);
  Register #(.width(4)) register_6 (
    .D(player_score_update[3:0]), .en(not_15_out), .Q(out_12), .clk(clock_t), .clr(reset));
  Counter #(.width(1), .max('h1), .ongoal("stay")) counter_9 (
    .Q(stop_P), .clk(and_8_out), .clr(reset));  // open: load, D, count, carry
  not not_17 (not_17_out, comparator_10_eq);
  or or_1 (or_1_out, reset, R_0_reset);
  or or_2 (or_2_out, reset, P_0_reset);
  Adder adder_5 (.a(BallX_PRE_SUM), .b(8'h1b), .out(adder_5_out));  // open: cin, cout
  and and_11 (right_reflect, C_right_flag, is_hit_the_left_2_out_3, not_18_out);
  not not_18 (not_18_out, Vx_PRE[7]);
  is_hit_the_left is_hit_the_left_2 (.in_1(BallY_PRE_SUM), .leftBat(out_10), .out_3(is_hit_the_left_2_out_3));
  Adder adder_6 (.a(Vx_PRE), .b(adder_5_out), .cout(C_right_flag));  // open: out, cin

  // Other names for the same wires on the sheet: RightBATEA[4:0] = out_10

  // Notes on the sheet:
  //   |
  //   |
  //   3bitX
  //   3bitY
  //   |
  //   |
  //   ___________________________
  //   WALLS
  //   _________________________
  //   Vy analyze
  //   ___________________________
  //   ___________________________
  //   |
  //   |
  //   Vx analyze
  //   ___________________________
  //   |
  //   |
  //   BATS
  //   _________________________
  //   robot won
  //   player won
  //   ___________________________
  //   |
  //   |
endmodule

module videoSub (
  input  [4:0] in_1,
  input  [4:0] in_2,
  input  [4:0] in_3,
  input  [4:0] in_4,
  input  [4:0] in_5,
  output [31:0] out_6,
  output [31:0] out_7,
  output [31:0] out_8,
  output [31:0] out_9,
  output [31:0] out_10,
  output [31:0] out_11,
  output [31:0] out_12,
  output [31:0] out_13,
  output [4:0] BallX,
  output [4:0] BallY,
  output [4:0] rightBat,
  output [4:0] leftBat,
  output [4:0] chipID
);

  wire [4:0] videochip_1_ballx_2, videochip_1_bally_2, videochip_1_chipid_2, videochip_1_leftbat_2,
       videochip_1_rightbat_2, videochip_2_ballx_2, videochip_2_bally_2, videochip_2_chipid_2,
       videochip_2_leftbat_2, videochip_2_rightbat_2, videochip_3_ballx_2, videochip_3_bally_2,
       videochip_3_chipid_2, videochip_3_leftbat_2, videochip_3_rightbat_2, videochip_4_ballx_2,
       videochip_4_bally_2, videochip_4_chipid_2, videochip_4_leftbat_2, videochip_4_rightbat_2,
       videochip_5_ballx_2, videochip_5_bally_2, videochip_5_chipid_2, videochip_5_leftbat_2,
       videochip_5_rightbat_2, videochip_6_ballx_2, videochip_6_bally_2, videochip_6_chipid_2,
       videochip_6_leftbat_2, videochip_6_rightbat_2, videochip_7_ballx_2, videochip_7_bally_2,
       videochip_7_chipid_2, videochip_7_leftbat_2, videochip_7_rightbat_2;

  videochip videochip_1 (
    .chipID(in_5), .leftBat(in_4), .rightBat(in_3), .BallY(in_2), .BallX(in_1),
    .BallX_2(videochip_1_ballx_2), .BallY_2(videochip_1_bally_2), .rightBat_2(videochip_1_rightbat_2),
    .leftBat_2(videochip_1_leftbat_2), .chipID_2(videochip_1_chipid_2), .out_6(out_6));
  videochip videochip_2 (
    .chipID(videochip_1_chipid_2), .leftBat(videochip_1_leftbat_2), .rightBat(videochip_1_rightbat_2),
    .BallY(videochip_1_bally_2), .BallX(videochip_1_ballx_2), .BallX_2(videochip_2_ballx_2),
    .BallY_2(videochip_2_bally_2), .rightBat_2(videochip_2_rightbat_2), .leftBat_2(videochip_2_leftbat_2),
    .chipID_2(videochip_2_chipid_2), .out_6(out_7));
  videochip videochip_3 (
    .chipID(videochip_2_chipid_2), .leftBat(videochip_2_leftbat_2), .rightBat(videochip_2_rightbat_2),
    .BallY(videochip_2_bally_2), .BallX(videochip_2_ballx_2), .BallX_2(videochip_3_ballx_2),
    .BallY_2(videochip_3_bally_2), .rightBat_2(videochip_3_rightbat_2), .leftBat_2(videochip_3_leftbat_2),
    .chipID_2(videochip_3_chipid_2), .out_6(out_8));
  videochip videochip_4 (
    .chipID(videochip_3_chipid_2), .leftBat(videochip_3_leftbat_2), .rightBat(videochip_3_rightbat_2),
    .BallY(videochip_3_bally_2), .BallX(videochip_3_ballx_2), .BallX_2(videochip_4_ballx_2),
    .BallY_2(videochip_4_bally_2), .rightBat_2(videochip_4_rightbat_2), .leftBat_2(videochip_4_leftbat_2),
    .chipID_2(videochip_4_chipid_2), .out_6(out_9));
  videochip videochip_5 (
    .chipID(videochip_4_chipid_2), .leftBat(videochip_4_leftbat_2), .rightBat(videochip_4_rightbat_2),
    .BallY(videochip_4_bally_2), .BallX(videochip_4_ballx_2), .BallX_2(videochip_5_ballx_2),
    .BallY_2(videochip_5_bally_2), .rightBat_2(videochip_5_rightbat_2), .leftBat_2(videochip_5_leftbat_2),
    .chipID_2(videochip_5_chipid_2), .out_6(out_10));
  videochip videochip_6 (
    .chipID(videochip_5_chipid_2), .leftBat(videochip_5_leftbat_2), .rightBat(videochip_5_rightbat_2),
    .BallY(videochip_5_bally_2), .BallX(videochip_5_ballx_2), .BallX_2(videochip_6_ballx_2),
    .BallY_2(videochip_6_bally_2), .rightBat_2(videochip_6_rightbat_2), .leftBat_2(videochip_6_leftbat_2),
    .chipID_2(videochip_6_chipid_2), .out_6(out_11));
  videochip videochip_7 (
    .chipID(videochip_6_chipid_2), .leftBat(videochip_6_leftbat_2), .rightBat(videochip_6_rightbat_2),
    .BallY(videochip_6_bally_2), .BallX(videochip_6_ballx_2), .BallX_2(videochip_7_ballx_2),
    .BallY_2(videochip_7_bally_2), .rightBat_2(videochip_7_rightbat_2), .leftBat_2(videochip_7_leftbat_2),
    .chipID_2(videochip_7_chipid_2), .out_6(out_12));
  videochip videochip_8 (
    .chipID(videochip_7_chipid_2), .leftBat(videochip_7_leftbat_2), .rightBat(videochip_7_rightbat_2),
    .BallY(videochip_7_bally_2), .BallX(videochip_7_ballx_2), .BallX_2(BallX), .BallY_2(BallY),
    .rightBat_2(rightBat), .leftBat_2(leftBat), .chipID_2(chipID), .out_6(out_13));
endmodule

module _3_bit_to_8_sign (
  input  [2:0] in_1,
  output [7:0] out_2
);

  wire [2:0] adder_1_out, not_1_out;
  wire [7:0] adder_2_out, not_2_out;

  assign not_1_out = ~in_1;  // NOT_Gate not_1, 3 bits wide
  Adder #(.width(3)) adder_1 (.a(not_1_out), .b(3'b001), .out(adder_1_out));  // open: cin, cout
  Multiplexer #(.width(8)) multiplexer_1 (
    .in0({{5{1'b0}}, in_1}), .in1(adder_2_out), .out(out_2), .sel(in_1[2]));  // open: en
  assign not_2_out = ~{{5{1'b0}}, adder_1_out};  // NOT_Gate not_2, 8 bits wide
  Adder adder_2 (.a(not_2_out), .b(8'h1), .out(adder_2_out));  // open: cin, cout
endmodule

module is_hit_the_left (
  input  [7:0] in_1,
  input  [4:0] leftBat,
  output out_3
);

  wire comparator_1_eq, comparator_2_eq, comparator_3_eq;
  wire [4:0] adder_1_out, adder_2_out, bit_extender_1_out;
  wire [7:0] shifter_1_out;

  Shifter #(.shift("lr")) shifter_1 (.in(in_1), .\dist (3'b011), .out(shifter_1_out));
  Bit_Extender #(.out_width(5)) bit_extender_1 (.in(shifter_1_out), .out(bit_extender_1_out));
  Adder #(.width(5)) adder_1 (.a(leftBat), .b(5'b00001), .out(adder_1_out));  // open: cin, cout
  Adder #(.width(5)) adder_2 (.a(leftBat), .b(5'b00010), .out(adder_2_out));  // open: cin, cout
  Comparator #(.width(5), .mode("unsigned")) comparator_1 (
    .a(bit_extender_1_out), .b(leftBat), .eq(comparator_1_eq));  // open: gt, lt
  Comparator #(.width(5), .mode("unsigned")) comparator_2 (
    .a(bit_extender_1_out), .b(adder_1_out), .eq(comparator_2_eq));  // open: gt, lt
  Comparator #(.width(5), .mode("unsigned")) comparator_3 (
    .a(bit_extender_1_out), .b(adder_2_out), .eq(comparator_3_eq));  // open: gt, lt
  or or_1 (out_3, comparator_1_eq, comparator_2_eq, comparator_3_eq);
endmodule

module is_hit_the_right (
  input  [7:0] in_1,
  input  [4:0] RIghtBat,
  output out_3
);

  wire comparator_1_eq, comparator_2_eq, comparator_3_eq;
  wire [4:0] adder_1_out, adder_2_out, bit_extender_1_out;
  wire [7:0] shifter_1_out;

  Shifter #(.shift("lr")) shifter_1 (.in(in_1), .\dist (3'b011), .out(shifter_1_out));
  Bit_Extender #(.out_width(5)) bit_extender_1 (.in(shifter_1_out), .out(bit_extender_1_out));
  Adder #(.width(5)) adder_1 (.a(RIghtBat), .b(5'b00001), .out(adder_1_out));  // open: cin, cout
  Adder #(.width(5)) adder_2 (.a(RIghtBat), .b(5'b00010), .out(adder_2_out));  // open: cin, cout
  Comparator #(.width(5), .mode("unsigned")) comparator_1 (
    .a(bit_extender_1_out), .b(RIghtBat), .eq(comparator_1_eq));  // open: gt, lt
  Comparator #(.width(5), .mode("unsigned")) comparator_2 (
    .a(bit_extender_1_out), .b(adder_1_out), .eq(comparator_2_eq));  // open: gt, lt
  Comparator #(.width(5), .mode("unsigned")) comparator_3 (
    .a(bit_extender_1_out), .b(adder_2_out), .eq(comparator_3_eq));  // open: gt, lt
  or or_1 (out_3, comparator_1_eq, comparator_2_eq, comparator_3_eq);
endmodule

module invert_V (
  input  [7:0] in_1,
  output [7:0] out_2
);

  wire comparator_1_eq;
  wire [7:0] adder_1_out, not_1_out;

  assign not_1_out = ~in_1;  // NOT_Gate not_1, 8 bits wide
  Comparator comparator_1 (.a(in_1), .b(8'hfc), .eq(comparator_1_eq));  // open: gt, lt
  Adder adder_1 (.a(not_1_out), .b(8'h1), .out(adder_1_out));  // open: cin, cout
  Multiplexer #(.width(8)) multiplexer_1 (
    .in0(adder_1_out), .in1(8'h3), .out(out_2), .sel(comparator_1_eq));  // open: en
endmodule

module _8_to_3 (
  input  [7:0] in_1,
  output [2:0] out_2
);

  wire [2:0] adder_2_out, bit_extender_1_out, bit_extender_2_out, not_2_out;
  wire [7:0] adder_1_out, not_1_out;

  assign not_1_out = ~in_1;  // NOT_Gate not_1, 8 bits wide
  Bit_Extender #(.out_width(3)) bit_extender_1 (.in(in_1), .out(bit_extender_1_out));
  Adder adder_1 (.a(not_1_out), .b(8'h1), .out(adder_1_out));  // open: cin, cout
  Multiplexer #(.width(3)) multiplexer_1 (
    .in0(bit_extender_1_out), .in1(adder_2_out), .out(out_2), .sel(in_1[7]));  // open: en
  assign not_2_out = ~bit_extender_2_out;  // NOT_Gate not_2, 3 bits wide
  Bit_Extender #(.out_width(3)) bit_extender_2 (.in(adder_1_out), .out(bit_extender_2_out));
  Adder #(.width(3)) adder_2 (.a(not_2_out), .b(3'b001), .out(adder_2_out));  // open: cin, cout
endmodule
