// Logisim project tennis_fin.circ as structural Verilog: 15 circuits, main circuit main
module main (
);

  wire button_out, clock_1_out, kinematic_controller_1_power_2, kinematic_controller_1_show_menu,
       kinematic_controller_1_stop, res, set_out, switch_1_out_2, videosub_1_game_over,
       videosub_1_is_in_menu, videosub_1_power, videosub_2_game_over, videosub_2_is_in_menu,
       videosub_2_power, videosub_3_game_over, videosub_3_is_in_menu, videosub_3_power;
  wire [1:0] kinematic_controller_1_result, videosub_1_game_result, videosub_2_game_result,
       videosub_3_game_result;
  wire [2:0] kinematic_controller_1_level, videosub_1_level, videosub_2_level, videosub_3_level;
  wire [3:0] P_0, P_1, R_0, R_1, T_0, T_1;
  wire [4:0] joystick_1_y, joystick_2_out_2, kinematic_controller_1_ballx, kinematic_controller_1_bally,
       kinematic_controller_1_joystick, kinematic_controller_1_robot, not_1_out, videosub_1_ballx,
       videosub_1_bally, videosub_1_chipid, videosub_1_leftbat, videosub_1_rightbat, videosub_2_ballx,
       videosub_2_bally, videosub_2_chipid, videosub_2_leftbat, videosub_2_rightbat, videosub_3_ballx,
       videosub_3_bally, videosub_3_chipid, videosub_3_leftbat, videosub_3_rightbat;
  wire [31:0] videosub_1_out_11, videosub_1_out_12, videosub_1_out_13, videosub_1_out_14, videosub_1_out_15,
       videosub_1_out_16, videosub_1_out_17, videosub_1_out_18, videosub_2_out_11, videosub_2_out_12,
       videosub_2_out_13, videosub_2_out_14, videosub_2_out_15, videosub_2_out_16, videosub_2_out_17,
       videosub_2_out_18, videosub_3_out_11, videosub_3_out_12, videosub_3_out_13, videosub_3_out_14,
       videosub_3_out_15, videosub_3_out_16, videosub_3_out_17, videosub_3_out_18, videosub_4_out_11,
       videosub_4_out_12, videosub_4_out_13, videosub_4_out_14, videosub_4_out_15, videosub_4_out_16,
       videosub_4_out_17, videosub_4_out_18;

  Button button (.out(button_out));
  switch switch_1 (.tap_here_x2(button_out), .out_2(switch_1_out_2));
  Button u_RES (.out(res));
  // Probe on joystick_1_y
  Joystick_part #(.bits(5)) joystick_1 (.y(joystick_1_y));  // open: x
  Button set (.out(set_out));
  Joystick joystick_2 (.in_1(joystick_1_y), .out_2(joystick_2_out_2));
  assign not_1_out = ~joystick_2_out_2;  // NOT_Gate not_1, 5 bits wide
  Kinematic_controller kinematic_controller_1 (
    .reset(res), .BallX(kinematic_controller_1_ballx), .BallY(kinematic_controller_1_bally),
    .clock(clock_1_out), .robot_r1(R_1), .robot_r0(R_0), .LeftBat(not_1_out),
    .JoyStick(kinematic_controller_1_joystick), .Robot(kinematic_controller_1_robot), .power(switch_1_out_2),
    .power_2(kinematic_controller_1_power_2), .Inputs(set_out), .show_menu(kinematic_controller_1_show_menu),
    .level(kinematic_controller_1_level), .player_r0(P_0), .timer_r1(T_1), .timer_r0(T_0), .player_r1(P_1),
    .stop(kinematic_controller_1_stop), .result(kinematic_controller_1_result));
  Clock clock_1 (.out(clock_1_out));
  // Probe on not_1_out
  Hex_Digit_Display hex_digit_display_1 (.value(P_1));  // open: dp
  videoSub videosub_1 (
    .out_11(videosub_1_out_11), .out_12(videosub_1_out_12), .out_13(videosub_1_out_13),
    .out_14(videosub_1_out_14), .out_15(videosub_1_out_15), .out_16(videosub_1_out_16),
    .out_17(videosub_1_out_17), .out_18(videosub_1_out_18), .in_1(kinematic_controller_1_ballx),
    .in_2(kinematic_controller_1_bally), .in_3(kinematic_controller_1_robot),
    .in_4(kinematic_controller_1_joystick), .in_5({5{1'b0}}), .BallX(videosub_1_ballx),
    .BallY(videosub_1_bally), .rightBat(videosub_1_rightbat), .leftBat(videosub_1_leftbat),
    .chipID(videosub_1_chipid), .in_6(kinematic_controller_1_power_2), .power(videosub_1_power),
    .in_7(kinematic_controller_1_show_menu), .in_8(kinematic_controller_1_level), .level(videosub_1_level),
    .is_in_menu(videosub_1_is_in_menu), .in_9(kinematic_controller_1_stop), .game_over(videosub_1_game_over),
    .in_10(kinematic_controller_1_result), .game_result(videosub_1_game_result));
  DotMatrix #(.matrixcols(32), .matrixrows(32)) dotmatrix_1 (
    .col0(videosub_1_out_11), .col1(videosub_1_out_12), .col2(videosub_1_out_13), .col3(videosub_1_out_14),
    .col4(videosub_1_out_15), .col5(videosub_1_out_16), .col6(videosub_1_out_17), .col7(videosub_1_out_18),
    .col8(videosub_2_out_11), .col9(videosub_2_out_12), .col10(videosub_2_out_13), .col11(videosub_2_out_14),
    .col12(videosub_2_out_15), .col13(videosub_2_out_16), .col14(videosub_2_out_17),
    .col15(videosub_2_out_18), .col16(videosub_3_out_11), .col17(videosub_3_out_12),
    .col18(videosub_3_out_13), .col19(videosub_3_out_14), .col20(videosub_3_out_15),
    .col21(videosub_3_out_16), .col22(videosub_3_out_17), .col23(videosub_3_out_18),
    .col24(videosub_4_out_11), .col25(videosub_4_out_12), .col26(videosub_4_out_13),
    .col27(videosub_4_out_14), .col28(videosub_4_out_15), .col29(videosub_4_out_16),
    .col30(videosub_4_out_17), .col31(videosub_4_out_18));
  Hex_Digit_Display hex_digit_display_2 (.value(P_0));  // open: dp
  videoSub videosub_2 (
    .out_11(videosub_2_out_11), .out_12(videosub_2_out_12), .out_13(videosub_2_out_13),
    .out_14(videosub_2_out_14), .out_15(videosub_2_out_15), .out_16(videosub_2_out_16),
    .out_17(videosub_2_out_17), .out_18(videosub_2_out_18), .in_1(videosub_1_ballx), .in_2(videosub_1_bally),
    .in_3(videosub_1_rightbat), .in_4(videosub_1_leftbat), .in_5(videosub_1_chipid),
    .BallX(videosub_2_ballx), .BallY(videosub_2_bally), .rightBat(videosub_2_rightbat),
    .leftBat(videosub_2_leftbat), .chipID(videosub_2_chipid), .in_6(videosub_1_power),
    .power(videosub_2_power), .in_7(videosub_1_is_in_menu), .in_8(videosub_1_level),
    .level(videosub_2_level), .is_in_menu(videosub_2_is_in_menu), .in_9(videosub_1_game_over),
    .game_over(videosub_2_game_over), .in_10(videosub_1_game_result), .game_result(videosub_2_game_result));
  Hex_Digit_Display hex_digit_display_3 (.value(T_0));  // open: dp
  Hex_Digit_Display hex_digit_display_4 (.value(T_1));  // open: dp
  videoSub videosub_3 (
    .out_11(videosub_3_out_11), .out_12(videosub_3_out_12), .out_13(videosub_3_out_13),
    .out_14(videosub_3_out_14), .out_15(videosub_3_out_15), .out_16(videosub_3_out_16),
    .out_17(videosub_3_out_17), .out_18(videosub_3_out_18), .in_1(videosub_2_ballx), .in_2(videosub_2_bally),
    .in_3(videosub_2_rightbat), .in_4(videosub_2_leftbat), .in_5(videosub_2_chipid),
    .BallX(videosub_3_ballx), .BallY(videosub_3_bally), .rightBat(videosub_3_rightbat),
    .leftBat(videosub_3_leftbat), .chipID(videosub_3_chipid), .in_6(videosub_2_power),
    .power(videosub_3_power), .in_7(videosub_2_is_in_menu), .in_8(videosub_2_level),
    .level(videosub_3_level), .is_in_menu(videosub_3_is_in_menu), .in_9(videosub_2_game_over),
    .game_over(videosub_3_game_over), .in_10(videosub_2_game_result), .game_result(videosub_3_game_result));
  Hex_Digit_Display hex_digit_display_5 (.value(R_1));  // open: dp
  videoSub videosub_4 (
    .out_11(videosub_4_out_11), .out_12(videosub_4_out_12), .out_13(videosub_4_out_13),
    .out_14(videosub_4_out_14), .out_15(videosub_4_out_15), .out_16(videosub_4_out_16),
    .out_17(videosub_4_out_17), .out_18(videosub_4_out_18), .in_1(videosub_3_ballx), .in_2(videosub_3_bally),
    .in_3(videosub_3_rightbat), .in_4(videosub_3_leftbat), .in_5(videosub_3_chipid), .in_6(videosub_3_power),
    .in_7(videosub_3_is_in_menu), .in_8(videosub_3_level), .in_9(videosub_3_game_over),
    .in_10(videosub_3_game_result));  // open: BallX, BallY, rightBat, leftBat, chipID, power, level, is_in_menu, game_over, game_result
  Hex_Digit_Display hex_digit_display_6 (.value(R_0));  // open: dp
endmodule

module Kinematic_controller (
  input  Inputs,
  input  [4:0] LeftBat,
  input  reset,
  input  clock,
  input  power,
  output [4:0] Robot,
  output [3:0] player_r1,
  output [3:0] player_r0,
  output [4:0] JoyStick,
  output [4:0] BallX,
  output [3:0] robot_r1,
  output [3:0] robot_r0,
  output [4:0] BallY,
  output [3:0] timer_r1,
  output [3:0] timer_r0,
  output power_2,
  output [1:0] result,
  output [2:0] level,
  output show_menu,
  output stop
);

  wire and_1_out, and_2_out, and_4_out, and_8_out, and_9_out, and_10_out, C_left_flag, C_right_flag, clock_t,
       comparator_1_gt, comparator_3_eq, comparator_3_gt, comparator_3_lt, comparator_5_lt, comparator_6_eq,
       comparator_6_gt, comparator_7_gt, comparator_8_eq, counter_1_q, counter_3_q, counter_4_q, counter_5_q,
       counter_7_q, is_hit_bat_1_hits_star, is_hit_bat_2_hits_star, left_reflect, level_1_no_start,
       multiplexer_1_out, multiplexer_2_out, multiplexer_5_out, multiplexer_6_out, NO_NAGIB, not_2_out,
       not_4_out, not_5_out, not_6_out, not_7_out, not_8_out, not_9_out, not_10_out, not_11_out, not_12_out,
       not_13_out, not_14_out, not_15_out, not_16_out, not_17_out, not_18_out, not_19_out, not_20_out,
       not_22_out, not_23_out, nrun_prime, P_stop, R_stop, reflect, reflect_t, reflectX, reset_t,
       right_reflect, timer, X_C_flag, Y_C_flag;
  wire [2:0] controlled_buffer_1_out, controlled_buffer_2_out, set_Vx, set_Vy;
  wire [4:0] controlled_buffer_5_out, controlled_buffer_6_out, controlled_buffer_10_out, RightBAT_smooth;
  wire [5:0] VXY_8bit;
  wire [7:0] adder_1_out, adder_2_out, adder_3_out, adder_6_out, adder_8_out, BallX_POST_sum, BallX_PRE_SUM,
       BallY_POST_sum, BallY_PRE_SUM, controlled_buffer_3_out, controlled_buffer_4_out,
       controlled_buffer_13_out, controlled_buffer_14_out, controlled_buffer_17_out, counter_8_q,
       difficulty_mechanics_1_right_bat_fin, divider_1_out, divider_1_rem, divider_2_out, divider_2_rem,
       divider_3_out, divider_3_rem, input_output_1_out_7, invert_v_1_out_2, invert_v_2_out_2,
       player_score_update, RightBAT_tmp, robot_score_update, shifter_1_out, shifter_2_out, shifter_3_out,
       subtractor_1_out, Vx_POST, Vx_PRE, Vy_POST, Vy_PRE;

  not not_1 (show_menu, level_1_no_start);
  Level level_1 (
    .res(reset_t), .set(Inputs), .in_3(LeftBat), .no_start(level_1_no_start), .hard(level[0]),
    .norm(level[1]), .ez(level[2]));
  assign controlled_buffer_1_out = show_menu ? set_Vx : 3'bz;  // Controlled_Buffer controlled_buffer_1
  _3_bit_to_8_sign u_3_bit_to_8_sign_1 (.in_1(controlled_buffer_1_out), .out_2(Vx_POST));
  assign controlled_buffer_2_out = show_menu ? set_Vy : 3'bz;  // Controlled_Buffer controlled_buffer_2
  _3_bit_to_8_sign u_3_bit_to_8_sign_2 (.in_1(controlled_buffer_2_out), .out_2(Vy_POST));
  or or_1 (reset_t, reset, not_2_out);
  not not_2 (not_2_out, power);
  Counter #(.width(1), .max('h1)) counter_1 (.Q(counter_1_q), .clk(clock));  // open: load, D, count, carry, clr
  Input_Output input_output_1 (
    .in_1({2'b00, VXY_8bit}), .out_7(input_output_1_out_7), .block(NO_NAGIB), .INPUT_BallX_8b(BallX_PRE_SUM),
    .INPUT_BallY_8b(BallY_PRE_SUM), .res(reset_t), .run(show_menu));
  not not_3 (nrun_prime, show_menu);
  Counter #(.width(1), .max('h1)) counter_2 (.Q(clock_t), .clk(counter_1_q));  // open: load, D, count, carry, clr
  Multiplexer multiplexer_1 (.in0(1'b0), .in1(1'b1), .out(multiplexer_1_out), .sel(Y_C_flag));  // open: en
  Multiplexer multiplexer_2 (.in0(1'b1), .in1(1'b0), .out(multiplexer_2_out), .sel(Y_C_flag));  // open: en
  Register register_1 (.D(Vx_POST), .Q(Vx_PRE), .clk(clock_t), .clr(reset_t));  // open: en
  Register register_2 (.D(Vy_POST), .Q(Vy_PRE), .clk(clock_t), .clr(reset_t));  // open: en
  Multiplexer multiplexer_3 (
    .in0(multiplexer_1_out), .in1(multiplexer_2_out), .out(reflect), .sel(Vy_PRE[7]));  // open: en
  Difficulty_mechanics difficulty_mechanics_1 (
    .level(level), .right_bat(RightBAT_tmp), .VY(set_Vy), .VX_2(set_Vx),
    .right_bat_fin(difficulty_mechanics_1_right_bat_fin), .ball_X(BallX_PRE_SUM), .VX({2'b00, VXY_8bit}));
  assign controlled_buffer_3_out = nrun_prime ? Vy_PRE : 8'bz;  // Controlled_Buffer controlled_buffer_3
  invert_V invert_v_1 (.in_1(Vy_PRE), .out_2(invert_v_1_out_2));
  Adder adder_1 (.a(input_output_1_out_7), .b(8'hf6), .out(adder_1_out));  // open: cin, cout
  Multiplexer #(.width(8), .enable("false")) multiplexer_4 (
    .in0(adder_1_out), .in1(input_output_1_out_7), .out(RightBAT_tmp), .sel(not_4_out));
  not not_4 (not_4_out, comparator_1_gt);
  Comparator #(.mode("unsigned")) comparator_1 (
    .a(input_output_1_out_7), .b(8'h10), .gt(comparator_1_gt));  // open: eq, lt
  Adder adder_2 (.a(Vx_PRE), .b(BallX_PRE_SUM), .out(adder_2_out), .cout(X_C_flag));  // open: cin
  Adder adder_3 (.a(BallY_PRE_SUM), .b(Vy_PRE), .out(adder_3_out), .cout(Y_C_flag));  // open: cin
  assign controlled_buffer_4_out = not_5_out ? controlled_buffer_3_out : 8'bz;  // Controlled_Buffer controlled_buffer_4
  not not_5 (not_5_out, reflect);
  and and_1 (and_1_out, reflect, not_6_out);
  not not_6 (not_6_out, clock_t);
  Multiplexer multiplexer_5 (.in0(1'b0), .in1(1'b1), .out(multiplexer_5_out), .sel(X_C_flag));  // open: en
  Multiplexer multiplexer_6 (.in0(1'b1), .in1(1'b0), .out(multiplexer_6_out), .sel(X_C_flag));  // open: en
  Comparator #(.mode("unsigned")) comparator_2 (.a(BallX_PRE_SUM), .b(8'h9f), .gt(NO_NAGIB));  // open: eq, lt
  assign controlled_buffer_5_out = comparator_3_gt ? Robot : 5'bz;  // Controlled_Buffer controlled_buffer_5
  Comparator #(.width(5), .mode("unsigned")) comparator_3 (
    .a(RightBAT_smooth), .b(Robot), .gt(comparator_3_gt), .eq(comparator_3_eq), .lt(comparator_3_lt));
  assign controlled_buffer_6_out = comparator_3_lt ? Robot : 5'bz;  // Controlled_Buffer controlled_buffer_6
  Shifter #(.shift("lr")) shifter_1 (.in(difficulty_mechanics_1_right_bat_fin), .\dist (3'b011), .out(shifter_1_out));
  assign BallX_POST_sum = nrun_prime ? adder_2_out : 8'bz;  // Controlled_Buffer controlled_buffer_7
  assign BallY_POST_sum = nrun_prime ? adder_3_out : 8'bz;  // Controlled_Buffer controlled_buffer_8
  assign Vy_POST = nrun_prime ? controlled_buffer_4_out : 8'bz;  // Controlled_Buffer controlled_buffer_9
  Multiplexer #(.width(8), .enable("false")) multiplexer_7 (
    .in0(Vy_PRE), .in1(invert_v_1_out_2), .out(controlled_buffer_4_out), .sel(and_1_out));
  Multiplexer multiplexer_8 (
    .in0(multiplexer_5_out), .in1(multiplexer_6_out), .out(reflect_t), .sel(Vx_PRE[7]));  // open: en
  assign controlled_buffer_10_out = comparator_3_eq ? Robot : 5'bz;  // Controlled_Buffer controlled_buffer_10
  Adder #(.width(5)) adder_4 (
    .a(controlled_buffer_5_out), .b(5'b00001), .out(controlled_buffer_10_out));  // open: cin, cout
  Adder #(.width(5)) adder_5 (
    .a(controlled_buffer_6_out), .b({5{1'b1}}), .out(controlled_buffer_10_out));  // open: cin, cout
  Bit_Extender #(.out_width(5)) bit_extender_1 (.in(shifter_1_out), .out(RightBAT_smooth));
  _8_to_3 u_8_to_3_1 (.in_1(Vx_POST), .out_2(VXY_8bit[2:0]));
  _8_to_3 u_8_to_3_2 (.in_1(Vy_POST), .out_2(VXY_8bit[5:3]));
  not not_7 (not_7_out, NO_NAGIB);
  Register #(.width(5)) register_3 (
    .D(controlled_buffer_10_out), .en(not_7_out), .Q(Robot), .clk(clock_t));  // open: clr
  assign BallX_POST_sum = show_menu ? 8'hbf : 8'bz;  // Controlled_Buffer controlled_buffer_11
  assign BallY_POST_sum = show_menu ? 8'h7f : 8'bz;  // Controlled_Buffer controlled_buffer_12
  assign controlled_buffer_13_out = nrun_prime ? Vx_PRE : 8'bz;  // Controlled_Buffer controlled_buffer_13
  assign controlled_buffer_14_out = not_8_out ? controlled_buffer_13_out : 8'bz;  // Controlled_Buffer controlled_buffer_14
  not not_8 (not_8_out, reflectX);
  invert_V invert_v_2 (.in_1(Vx_PRE), .out_2(invert_v_2_out_2));
  not not_9 (not_9_out, left_reflect);
  and and_2 (and_2_out, not_9_out, not_10_out, not_11_out);
  not not_10 (not_10_out, reflect_t);
  not not_11 (not_11_out, right_reflect);
  Register register_4 (.D(BallX_POST_sum), .en(not_12_out), .Q(BallX_PRE_SUM), .clk(clock_t), .clr(reset_t));
  not not_12 (not_12_out, reflect_t);
  Register register_5 (.D(BallY_POST_sum), .en(not_13_out), .Q(BallY_PRE_SUM), .clk(clock_t), .clr(reset_t));
  not not_13 (not_13_out, reflect);
  assign Vx_POST = nrun_prime ? controlled_buffer_14_out : 8'bz;  // Controlled_Buffer controlled_buffer_15
  Multiplexer #(.width(8), .enable("false")) multiplexer_9 (
    .in0(Vx_PRE), .in1(invert_v_2_out_2), .out(controlled_buffer_14_out), .sel(reflectX));
  not not_14 (not_14_out, and_2_out);
  not not_15 (not_15_out, clock_t);
  and and_3 (reflectX, not_14_out, not_15_out);
  Adder adder_6 (.a(BallX_PRE_SUM), .b(8'he4), .out(adder_6_out));  // open: cin, cout
  not not_16 (not_16_out, C_left_flag);
  is_hit_bat is_hit_bat_1 (.BallY(BallY_PRE_SUM), .hits_star(is_hit_bat_1_hits_star), .Bat(LeftBat));
  and and_4 (and_4_out, nrun_prime, not_17_out);
  not not_17 (not_17_out, stop);
  Counter #(.width(1), .max('h1)) counter_3 (.Q(counter_3_q), .clk(counter_4_q));  // open: load, D, count, carry, clr
  Counter #(.width(1), .max('h1)) counter_4 (.Q(counter_4_q), .clk(counter_5_q));  // open: load, D, count, carry, clr
  Counter #(.width(1), .max('h1)) counter_5 (.Q(counter_5_q), .clk(clock_t));  // open: load, D, count, carry, clr
  Adder adder_7 (.a(Vx_PRE), .b(adder_6_out), .cout(C_left_flag));  // open: out, cin
  and and_5 (left_reflect, not_16_out, is_hit_bat_1_hits_star, Vx_PRE[7]);
  Counter #(.width(1), .max('h1)) counter_6 (.Q(timer), .clk(counter_7_q));  // open: load, D, count, carry, clr
  Counter #(.width(1), .max('h1)) counter_7 (.Q(counter_7_q), .clk(counter_3_q));  // open: load, D, count, carry, clr
  Controlled_Buffer #(.width(8)) controlled_buffer_16 (.in(subtractor_1_out), .en(nrun_prime));  // open: out
  not not_18 (not_18_out, stop);
  Counter counter_8 (
    .load(not_18_out), .D(controlled_buffer_17_out), .count(and_4_out), .Q(counter_8_q), .clk(timer));  // open: carry, clr
  assign controlled_buffer_17_out = show_menu ? 8'h63 : 8'bz;  // Controlled_Buffer controlled_buffer_17
  Shifter #(.shift("lr")) shifter_2 (.in(BallX_PRE_SUM), .\dist (3'b011), .out(shifter_2_out));
  Shifter #(.shift("lr")) shifter_3 (.in(BallY_PRE_SUM), .\dist (3'b011), .out(shifter_3_out));
  Comparator comparator_4 (.a(player_score_update), .b(8'h63), .eq(P_stop));  // open: gt, lt
  Divider divider_1 (.a(player_score_update), .b(8'ha), .out(divider_1_out), .rem(divider_1_rem));  // open: upper
  Comparator #(.mode("unsigned")) comparator_5 (.a(BallX_POST_sum), .b(8'h15), .lt(comparator_5_lt));  // open: gt, eq
  Comparator #(.mode("unsigned")) comparator_6 (
    .a(player_score_update), .b(robot_score_update), .gt(comparator_6_gt), .eq(comparator_6_eq));  // open: lt
  Bit_Extender #(.out_width(5)) bit_extender_2 (.in(shifter_2_out), .out(BallX));
  Bit_Extender #(.out_width(5)) bit_extender_3 (.in(shifter_3_out), .out(BallY));
  Bit_Extender #(.out_width(4)) bit_extender_4 (.in(divider_1_out), .out(player_r1));
  Comparator #(.mode("unsigned")) comparator_7 (.a(BallX_POST_sum), .b(8'he9), .gt(comparator_7_gt));  // open: eq, lt
  Adder adder_8 (.a(BallX_PRE_SUM), .b(8'h1b), .out(adder_8_out));  // open: cin, cout
  and and_6 (right_reflect, C_right_flag, is_hit_bat_2_hits_star, not_19_out);
  not not_19 (not_19_out, Vx_PRE[7]);
  is_hit_bat is_hit_bat_2 (.BallY(BallY_PRE_SUM), .hits_star(is_hit_bat_2_hits_star), .Bat(Robot));
  Subtractor subtractor_1 (.a(counter_8_q), .b(8'h1), .out(subtractor_1_out));  // open: bin, bout
  and and_7 (stop, nrun_prime, comparator_8_eq);
  Comparator #(.mode("unsigned")) comparator_8 (.a(counter_8_q), .b({8{1'b0}}), .eq(comparator_8_eq));  // open: gt, lt
  Bit_Extender #(.out_width(4)) bit_extender_5 (.in(divider_2_out), .out(timer_r1));
  Divider divider_2 (.a(counter_8_q), .b(8'ha), .out(divider_2_out), .rem(divider_2_rem));  // open: upper
  Bit_Extender #(.out_width(4)) bit_extender_6 (.in(divider_2_rem), .out(timer_r0));
  and and_8 (and_8_out, comparator_6_eq, level[0]);
  Bit_Extender #(.out_width(4)) bit_extender_7 (.in(divider_1_rem), .out(player_r0));
  and and_9 (and_9_out, ~R_stop, reflect_t, comparator_5_lt, not_20_out);  // AND_Gate
  not not_20 (not_20_out, X_C_flag);
  and and_10 (and_10_out, X_C_flag, comparator_7_gt, reflect_t, ~P_stop);  // AND_Gate
  Adder adder_9 (.a(Vx_PRE), .b(adder_8_out), .cout(C_right_flag));  // open: out, cin
  or or_2 (result[0], comparator_6_gt, and_8_out);
  not not_21 (result[1], result[0]);
  Comparator comparator_9 (.a(robot_score_update), .b(8'h63), .eq(R_stop));  // open: gt, lt
  Divider divider_3 (.a(robot_score_update), .b(8'ha), .out(divider_3_out), .rem(divider_3_rem));  // open: upper
  Counter #(.ongoal("load")) counter_9 (
    .count(not_22_out), .Q(robot_score_update), .clk(and_9_out), .clr(reset_t));  // open: load, D, carry
  not not_22 (not_22_out, stop);
  Counter #(.ongoal("load")) counter_10 (
    .count(not_23_out), .Q(player_score_update), .clk(and_10_out), .clr(reset_t));  // open: load, D, carry
  not not_23 (not_23_out, stop);
  Bit_Extender #(.out_width(4)) bit_extender_8 (.in(divider_3_out), .out(robot_r1));
  Bit_Extender #(.out_width(4)) bit_extender_9 (.in(divider_3_rem), .out(robot_r0));

  assign JoyStick = LeftBat;
  assign power_2 = power;

  // Other names for the same wires on the sheet: game_over = stop; game_result[1:0] = result; P_0[3:0] = player_r0;
  //   P_1[3:0] = player_r1; R_0[3:0] = robot_r0; R_1[3:0] = robot_r1; RightBATEA[4:0] = Robot; run = show_menu;
  //   set_level = Inputs; T_0[3:0] = timer_r0; T_1[3:0] = timer_r1

  // Notes on the sheet:
  //   3bitX
  //   3bitY
  //   |
  //   |
  //   players selects diff level
  //   Levels of diff + menu of sel flag
  //   because of calculation depends on bottom of bat
  //   game itself
  //   |
  //   |
  //   ___________________________
  //   moves rght bat a little bit down -->
  //   ______________________________________________________
  //   _______________
  //   WALLS
  //   _________________________
  //   Vy analyze
  //   block bat
  //   animates rght bat's movements
  //   ___________________________
  //   BallX
  //   BallY
  //   ___________________________
  //   ______________________________________________________
  //   |
  //   |
  //   output
  //   Vx analyze
  //   ___________________________
  //   _______________
  //   |
  //   |
  //   |
  //   |
  //   |
  //   |
  //   |
  //   |
  //   |
  //   BATS
  //   for left
  //   _________________________
  //   __________________
  //   __________________
  //   ___________________________
  //   Outputs
  //   Score 
  //   ___________________________
  //   for right
  //   __________________
  //   ___________________________
  //   ___________________________
  //   |
  //   |
  //   |
  //   |
  //   |
  //   |
  //   robot won
  //   player won
endmodule

module Videochip (
  input  [4:0] BallX,
  input  [4:0] BallY,
  input  [4:0] rightBat,
  input  [4:0] leftBat,
  input  [4:0] chipID,
  input  Power,
  input  menu,
  input  [2:0] lev_prime,
  input  game_over,
  input  [1:0] res,
  output [31:0] out_11,
  output [4:0] BallX_2,
  output [4:0] BallY_2,
  output [4:0] rightBat_2,
  output [4:0] leftBat_2,
  output [4:0] chipID_2,
  output Power_2,
  output out_18,
  output [2:0] out_19,
  output out_20,
  output [1:0] res_2
);

  wire comparator_1_eq, comparator_2_eq, comparator_3_eq;
  wire [31:0] decoder_1_out0, decoder_2_out0, decoder_3_out0, game_over_data, menu_data, multiplexer_2_out,
       multiplexer_3_out, multiplexer_4_out, multiplexer_5_out, multiplexer_6_out, or_1_out, or_2_out,
       or_3_out, shifter_1_out, shifter_2_out, shifter_3_out, shifter_4_out;

  Game_over_graphics game_over_graphics_1 (.chip_id(chipID), .game_resault(res), .out_3(game_over_data));
  Menu_graphics menu_graphics_1 (.chip_id(chipID), .level(lev_prime), .out_3(menu_data));
  Adder #(.width(5)) adder_1 (.a(chipID), .b(5'b00001), .out(chipID_2));  // open: cin, cout
  Comparator #(.width(5), .mode("unsigned")) comparator_1 (
    .a(BallX), .b(chipID), .eq(comparator_1_eq));  // open: gt, lt
  Comparator #(.width(5), .mode("unsigned")) comparator_2 (
    .a(chipID), .b(5'b00011), .eq(comparator_2_eq));  // open: gt, lt
  Comparator #(.width(5), .mode("unsigned")) comparator_3 (
    .a(chipID), .b(5'b11100), .eq(comparator_3_eq));  // open: gt, lt
  // Probe on 5'b11100
  Decoder #(.select(5), .enable("false")) decoder_1 (
    .out0(decoder_1_out0[0]), .out1(decoder_1_out0[1]), .out2(decoder_1_out0[2]), .out3(decoder_1_out0[3]),
    .out4(decoder_1_out0[4]), .out5(decoder_1_out0[5]), .out6(decoder_1_out0[6]), .out7(decoder_1_out0[7]),
    .out8(decoder_1_out0[8]), .out9(decoder_1_out0[9]), .out10(decoder_1_out0[10]),
    .out11(decoder_1_out0[11]), .out12(decoder_1_out0[12]), .out13(decoder_1_out0[13]),
    .out14(decoder_1_out0[14]), .out15(decoder_1_out0[15]), .out16(decoder_1_out0[16]),
    .out17(decoder_1_out0[17]), .out18(decoder_1_out0[18]), .out19(decoder_1_out0[19]),
    .out20(decoder_1_out0[20]), .out21(decoder_1_out0[21]), .out22(decoder_1_out0[22]),
    .out23(decoder_1_out0[23]), .out24(decoder_1_out0[24]), .out25(decoder_1_out0[25]),
    .out26(decoder_1_out0[26]), .out27(decoder_1_out0[27]), .out28(decoder_1_out0[28]),
    .out29(decoder_1_out0[29]), .out30(decoder_1_out0[30]), .out31(decoder_1_out0[31]), .sel(rightBat));
  Decoder #(.select(5), .enable("false")) decoder_2 (
    .out0(decoder_2_out0[0]), .out1(decoder_2_out0[1]), .out2(decoder_2_out0[2]), .out3(decoder_2_out0[3]),
    .out4(decoder_2_out0[4]), .out5(decoder_2_out0[5]), .out6(decoder_2_out0[6]), .out7(decoder_2_out0[7]),
    .out8(decoder_2_out0[8]), .out9(decoder_2_out0[9]), .out10(decoder_2_out0[10]),
    .out11(decoder_2_out0[11]), .out12(decoder_2_out0[12]), .out13(decoder_2_out0[13]),
    .out14(decoder_2_out0[14]), .out15(decoder_2_out0[15]), .out16(decoder_2_out0[16]),
    .out17(decoder_2_out0[17]), .out18(decoder_2_out0[18]), .out19(decoder_2_out0[19]),
    .out20(decoder_2_out0[20]), .out21(decoder_2_out0[21]), .out22(decoder_2_out0[22]),
    .out23(decoder_2_out0[23]), .out24(decoder_2_out0[24]), .out25(decoder_2_out0[25]),
    .out26(decoder_2_out0[26]), .out27(decoder_2_out0[27]), .out28(decoder_2_out0[28]),
    .out29(decoder_2_out0[29]), .out30(decoder_2_out0[30]), .out31(decoder_2_out0[31]), .sel(BallY));
  Decoder #(.select(5), .enable("false")) decoder_3 (
    .out0(decoder_3_out0[0]), .out1(decoder_3_out0[1]), .out2(decoder_3_out0[2]), .out3(decoder_3_out0[3]),
    .out4(decoder_3_out0[4]), .out5(decoder_3_out0[5]), .out6(decoder_3_out0[6]), .out7(decoder_3_out0[7]),
    .out8(decoder_3_out0[8]), .out9(decoder_3_out0[9]), .out10(decoder_3_out0[10]),
    .out11(decoder_3_out0[11]), .out12(decoder_3_out0[12]), .out13(decoder_3_out0[13]),
    .out14(decoder_3_out0[14]), .out15(decoder_3_out0[15]), .out16(decoder_3_out0[16]),
    .out17(decoder_3_out0[17]), .out18(decoder_3_out0[18]), .out19(decoder_3_out0[19]),
    .out20(decoder_3_out0[20]), .out21(decoder_3_out0[21]), .out22(decoder_3_out0[22]),
    .out23(decoder_3_out0[23]), .out24(decoder_3_out0[24]), .out25(decoder_3_out0[25]),
    .out26(decoder_3_out0[26]), .out27(decoder_3_out0[27]), .out28(decoder_3_out0[28]),
    .out29(decoder_3_out0[29]), .out30(decoder_3_out0[30]), .out31(decoder_3_out0[31]), .sel(leftBat));
  Multiplexer #(.width(32), .enable("false")) multiplexer_1 (
    .in0({32{1'b1}}), .in1(multiplexer_2_out), .out(out_11), .sel(Power));
  Multiplexer #(.width(32), .enable("false")) multiplexer_2 (
    .in0(multiplexer_3_out), .in1(game_over_data), .out(multiplexer_2_out), .sel(game_over));
  Multiplexer #(.width(32), .enable("false")) multiplexer_3 (
    .in0(or_3_out), .in1(menu_data), .out(multiplexer_3_out), .sel(menu));
  Multiplexer #(.width(32), .enable("false")) multiplexer_4 (
    .in0({32{1'b0}}), .in1(decoder_2_out0), .out(multiplexer_4_out), .sel(comparator_1_eq));
  Multiplexer #(.width(32), .enable("false")) multiplexer_5 (
    .in0({32{1'b0}}), .in1(decoder_3_out0), .out(multiplexer_5_out), .sel(comparator_2_eq));
  Multiplexer #(.width(32), .enable("false")) multiplexer_6 (
    .in0({32{1'b0}}), .in1(decoder_1_out0), .out(multiplexer_6_out), .sel(comparator_3_eq));
  Shifter #(.width(32)) shifter_1 (.in(multiplexer_5_out), .\dist (5'b00001), .out(shifter_1_out));
  Shifter #(.width(32)) shifter_2 (.in(multiplexer_6_out), .\dist (5'b00001), .out(shifter_2_out));
  Shifter #(.width(32)) shifter_3 (.in(shifter_1_out), .\dist (5'b00001), .out(shifter_3_out));
  Shifter #(.width(32)) shifter_4 (.in(shifter_2_out), .\dist (5'b00001), .out(shifter_4_out));
  assign or_1_out = multiplexer_5_out | shifter_1_out | shifter_3_out;  // OR_Gate or_1, 32 bits wide
  assign or_2_out = multiplexer_6_out | shifter_2_out | shifter_4_out;  // OR_Gate or_2, 32 bits wide
  assign or_3_out = multiplexer_4_out | or_1_out | or_2_out;  // OR_Gate or_3, 32 bits wide

  assign BallX_2 = BallX;
  assign BallY_2 = BallY;
  assign leftBat_2 = leftBat;
  assign out_18 = menu;
  assign out_19 = lev_prime;
  assign out_20 = game_over;
  assign Power_2 = Power;
  assign res_2 = res;
  assign rightBat_2 = rightBat;

  // Other names for the same wires on the sheet: level[2:0] = lev_prime

  // Notes on the sheet:
  //   Game over graphics
  //   Menu graphics
  //   no power -> only 1's (black pixels in our case)
endmodule

module videoSub (
  input  [4:0] in_1,
  input  [4:0] in_2,
  input  [4:0] in_3,
  input  [4:0] in_4,
  input  [4:0] in_5,
  input  in_6,
  input  in_7,
  input  [2:0] in_8,
  input  in_9,
  input  [1:0] in_10,
  output [31:0] out_11,
  output [31:0] out_12,
  output [31:0] out_13,
  output [31:0] out_14,
  output [31:0] out_15,
  output [31:0] out_16,
  output [31:0] out_17,
  output [31:0] out_18,
  output [4:0] BallX,
  output [4:0] BallY,
  output [4:0] rightBat,
  output [4:0] leftBat,
  output [4:0] chipID,
  output power,
  output [2:0] level,
  output is_in_menu,
  output [1:0] game_result,
  output game_over
);

  wire videochip_1_out_18, videochip_1_out_20, videochip_1_power_2, videochip_2_out_18, videochip_2_out_20,
       videochip_2_power_2, videochip_3_out_18, videochip_3_out_20, videochip_3_power_2, videochip_4_out_18,
       videochip_4_out_20, videochip_4_power_2, videochip_5_out_18, videochip_5_out_20, videochip_5_power_2,
       videochip_6_out_18, videochip_6_out_20, videochip_6_power_2, videochip_7_out_18, videochip_7_out_20,
       videochip_7_power_2;
  wire [1:0] videochip_1_res_2, videochip_2_res_2, videochip_3_res_2, videochip_4_res_2, videochip_5_res_2,
       videochip_6_res_2, videochip_7_res_2;
  wire [2:0] videochip_1_out_19, videochip_2_out_19, videochip_3_out_19, videochip_4_out_19,
       videochip_5_out_19, videochip_6_out_19, videochip_7_out_19;
  wire [4:0] videochip_1_ballx_2, videochip_1_bally_2, videochip_1_chipid_2, videochip_1_leftbat_2,
       videochip_1_rightbat_2, videochip_2_ballx_2, videochip_2_bally_2, videochip_2_chipid_2,
       videochip_2_leftbat_2, videochip_2_rightbat_2, videochip_3_ballx_2, videochip_3_bally_2,
       videochip_3_chipid_2, videochip_3_leftbat_2, videochip_3_rightbat_2, videochip_4_ballx_2,
       videochip_4_bally_2, videochip_4_chipid_2, videochip_4_leftbat_2, videochip_4_rightbat_2,
       videochip_5_ballx_2, videochip_5_bally_2, videochip_5_chipid_2, videochip_5_leftbat_2,
       videochip_5_rightbat_2, videochip_6_ballx_2, videochip_6_bally_2, videochip_6_chipid_2,
       videochip_6_leftbat_2, videochip_6_rightbat_2, videochip_7_ballx_2, videochip_7_bally_2,
       videochip_7_chipid_2, videochip_7_leftbat_2, videochip_7_rightbat_2;

  Videochip videochip_1 (
    .chipID(in_5), .leftBat(in_4), .rightBat(in_3), .BallY(in_2), .BallX(in_1),
    .BallX_2(videochip_1_ballx_2), .BallY_2(videochip_1_bally_2), .rightBat_2(videochip_1_rightbat_2),
    .leftBat_2(videochip_1_leftbat_2), .chipID_2(videochip_1_chipid_2), .out_11(out_11), .Power(in_6),
    .Power_2(videochip_1_power_2), .menu(in_7), .lev_prime(in_8), .out_18(videochip_1_out_18),
    .out_19(videochip_1_out_19), .game_over(in_9), .res(in_10), .out_20(videochip_1_out_20),
    .res_2(videochip_1_res_2));
  Videochip videochip_2 (
    .chipID(videochip_1_chipid_2), .leftBat(videochip_1_leftbat_2), .rightBat(videochip_1_rightbat_2),
    .BallY(videochip_1_bally_2), .BallX(videochip_1_ballx_2), .BallX_2(videochip_2_ballx_2),
    .BallY_2(videochip_2_bally_2), .rightBat_2(videochip_2_rightbat_2), .leftBat_2(videochip_2_leftbat_2),
    .chipID_2(videochip_2_chipid_2), .out_11(out_12), .Power(videochip_1_power_2),
    .Power_2(videochip_2_power_2), .menu(videochip_1_out_18), .lev_prime(videochip_1_out_19),
    .out_18(videochip_2_out_18), .out_19(videochip_2_out_19), .game_over(videochip_1_out_20),
    .res(videochip_1_res_2), .out_20(videochip_2_out_20), .res_2(videochip_2_res_2));
  Videochip videochip_3 (
    .chipID(videochip_2_chipid_2), .leftBat(videochip_2_leftbat_2), .rightBat(videochip_2_rightbat_2),
    .BallY(videochip_2_bally_2), .BallX(videochip_2_ballx_2), .BallX_2(videochip_3_ballx_2),
    .BallY_2(videochip_3_bally_2), .rightBat_2(videochip_3_rightbat_2), .leftBat_2(videochip_3_leftbat_2),
    .chipID_2(videochip_3_chipid_2), .out_11(out_13), .Power(videochip_2_power_2),
    .Power_2(videochip_3_power_2), .menu(videochip_2_out_18), .lev_prime(videochip_2_out_19),
    .out_18(videochip_3_out_18), .out_19(videochip_3_out_19), .game_over(videochip_2_out_20),
    .res(videochip_2_res_2), .out_20(videochip_3_out_20), .res_2(videochip_3_res_2));
  Videochip videochip_4 (
    .chipID(videochip_3_chipid_2), .leftBat(videochip_3_leftbat_2), .rightBat(videochip_3_rightbat_2),
    .BallY(videochip_3_bally_2), .BallX(videochip_3_ballx_2), .BallX_2(videochip_4_ballx_2),
    .BallY_2(videochip_4_bally_2), .rightBat_2(videochip_4_rightbat_2), .leftBat_2(videochip_4_leftbat_2),
    .chipID_2(videochip_4_chipid_2), .out_11(out_14), .Power(videochip_3_power_2),
    .Power_2(videochip_4_power_2), .menu(videochip_3_out_18), .lev_prime(videochip_3_out_19),
    .out_18(videochip_4_out_18), .out_19(videochip_4_out_19), .game_over(videochip_3_out_20),
    .res(videochip_3_res_2), .out_20(videochip_4_out_20), .res_2(videochip_4_res_2));
  Videochip videochip_5 (
    .chipID(videochip_4_chipid_2), .leftBat(videochip_4_leftbat_2), .rightBat(videochip_4_rightbat_2),
    .BallY(videochip_4_bally_2), .BallX(videochip_4_ballx_2), .BallX_2(videochip_5_ballx_2),
    .BallY_2(videochip_5_bally_2), .rightBat_2(videochip_5_rightbat_2), .leftBat_2(videochip_5_leftbat_2),
    .chipID_2(videochip_5_chipid_2), .out_11(out_15), .Power(videochip_4_power_2),
    .Power_2(videochip_5_power_2), .menu(videochip_4_out_18), .lev_prime(videochip_4_out_19),
    .out_18(videochip_5_out_18), .out_19(videochip_5_out_19), .game_over(videochip_4_out_20),
    .res(videochip_4_res_2), .out_20(videochip_5_out_20), .res_2(videochip_5_res_2));
  Videochip videochip_6 (
    .chipID(videochip_5_chipid_2), .leftBat(videochip_5_leftbat_2), .rightBat(videochip_5_rightbat_2),
    .BallY(videochip_5_bally_2), .BallX(videochip_5_ballx_2), .BallX_2(videochip_6_ballx_2),
    .BallY_2(videochip_6_bally_2), .rightBat_2(videochip_6_rightbat_2), .leftBat_2(videochip_6_leftbat_2),
    .chipID_2(videochip_6_chipid_2), .out_11(out_16), .Power(videochip_5_power_2),
    .Power_2(videochip_6_power_2), .menu(videochip_5_out_18), .lev_prime(videochip_5_out_19),
    .out_18(videochip_6_out_18), .out_19(videochip_6_out_19), .game_over(videochip_5_out_20),
    .res(videochip_5_res_2), .out_20(videochip_6_out_20), .res_2(videochip_6_res_2));
  Videochip videochip_7 (
    .chipID(videochip_6_chipid_2), .leftBat(videochip_6_leftbat_2), .rightBat(videochip_6_rightbat_2),
    .BallY(videochip_6_bally_2), .BallX(videochip_6_ballx_2), .BallX_2(videochip_7_ballx_2),
    .BallY_2(videochip_7_bally_2), .rightBat_2(videochip_7_rightbat_2), .leftBat_2(videochip_7_leftbat_2),
    .chipID_2(videochip_7_chipid_2), .out_11(out_17), .Power(videochip_6_power_2),
    .Power_2(videochip_7_power_2), .menu(videochip_6_out_18), .lev_prime(videochip_6_out_19),
    .out_18(videochip_7_out_18), .out_19(videochip_7_out_19), .game_over(videochip_6_out_20),
    .res(videochip_6_res_2), .out_20(videochip_7_out_20), .res_2(videochip_7_res_2));
  Videochip videochip_8 (
    .chipID(videochip_7_chipid_2), .leftBat(videochip_7_leftbat_2), .rightBat(videochip_7_rightbat_2),
    .BallY(videochip_7_bally_2), .BallX(videochip_7_ballx_2), .BallX_2(BallX), .BallY_2(BallY),
    .rightBat_2(rightBat), .leftBat_2(leftBat), .chipID_2(chipID), .out_11(out_18),
    .Power(videochip_7_power_2), .Power_2(power), .menu(videochip_7_out_18), .lev_prime(videochip_7_out_19),
    .out_18(is_in_menu), .out_19(level), .game_over(videochip_7_out_20), .res(videochip_7_res_2),
    .out_20(game_over), .res_2(game_result));
endmodule

module _3_bit_to_8_sign (
  input  [2:0] in_1,
  output [7:0] out_2
);

  wire [2:0] adder_1_out, not_1_out;
  wire [7:0] adder_2_out, not_2_out;

  assign not_1_out = ~in_1;  // NOT_Gate not_1, 3 bits wide
  Adder #(.width(3)) adder_1 (.a(not_1_out), .b(3'b001), .out(adder_1_out));  // open: cin, cout
  Multiplexer #(.width(8)) multiplexer_1 (
    .in0({{5{1'b0}}, in_1}), .in1(adder_2_out), .out(out_2), .sel(in_1[2]));  // open: en
  assign not_2_out = ~{{5{1'b0}}, adder_1_out};  // NOT_Gate not_2, 8 bits wide
  Adder adder_2 (.a(not_2_out), .b(8'h1), .out(adder_2_out));  // open: cin, cout
endmodule

module is_hit_bat (
  input  [7:0] BallY,
  input  [4:0] Bat,
  output hits_star
);

  wire comparator_1_eq, comparator_2_eq, comparator_3_eq;
  wire [4:0] adder_1_out, adder_2_out, bit_extender_1_out;
  wire [7:0] shifter_1_out;

  Shifter #(.shift("lr")) shifter_1 (.in(BallY), .\dist (3'b011), .out(shifter_1_out));
  Bit_Extender #(.out_width(5)) bit_extender_1 (.in(shifter_1_out), .out(bit_extender_1_out));
  Adder #(.width(5)) adder_1 (.a(Bat), .b(5'b00001), .out(adder_1_out));  // open: cin, cout
  Adder #(.width(5)) adder_2 (.a(Bat), .b(5'b00010), .out(adder_2_out));  // open: cin, cout
  Comparator #(.width(5), .mode("unsigned")) comparator_1 (
    .a(bit_extender_1_out), .b(Bat), .eq(comparator_1_eq));  // open: gt, lt
  Comparator #(.width(5), .mode("unsigned")) comparator_2 (
    .a(bit_extender_1_out), .b(adder_1_out), .eq(comparator_2_eq));  // open: gt, lt
  Comparator #(.width(5), .mode("unsigned")) comparator_3 (
    .a(bit_extender_1_out), .b(adder_2_out), .eq(comparator_3_eq));  // open: gt, lt
  or or_1 (hits_star, comparator_1_eq, comparator_2_eq, comparator_3_eq);
endmodule

module invert_V (
  input  [7:0] in_1,
  output [7:0] out_2
);

  wire comparator_1_eq;
  wire [7:0] adder_1_out, not_1_out;

  assign not_1_out = ~in_1;  // NOT_Gate not_1, 8 bits wide
  Comparator comparator_1 (.a(in_1), .b(8'hfc), .eq(comparator_1_eq));  // open: gt, lt
  Adder adder_1 (.a(not_1_out), .b(8'h1), .out(adder_1_out));  // open: cin, cout
  Multiplexer #(.width(8)) multiplexer_1 (
    .in0(adder_1_out), .in1(8'h3), .out(out_2), .sel(comparator_1_eq));  // open: en
endmodule

module _8_to_3 (
  input  [7:0] in_1,
  output [2:0] out_2
);

  wire [2:0] adder_2_out, bit_extender_1_out, bit_extender_2_out, not_2_out;
  wire [7:0] adder_1_out, not_1_out;

  assign not_1_out = ~in_1;  // NOT_Gate not_1, 8 bits wide
  Bit_Extender #(.out_width(3)) bit_extender_1 (.in(in_1), .out(bit_extender_1_out));
  Adder adder_1 (.a(not_1_out), .b(8'h1), .out(adder_1_out));  // open: cin, cout
  Multiplexer #(.width(3)) multiplexer_1 (
    .in0(bit_extender_1_out), .in1(adder_2_out), .out(out_2), .sel(in_1[7]));  // open: en
  assign not_2_out = ~bit_extender_2_out;  // NOT_Gate not_2, 3 bits wide
  Bit_Extender #(.out_width(3)) bit_extender_2 (.in(adder_1_out), .out(bit_extender_2_out));
  Adder #(.width(3)) adder_2 (.a(not_2_out), .b(3'b001), .out(adder_2_out));  // open: cin, cout
endmodule

module Input_Output (
  input  [7:0] in_1,
  input  block,
  input  [7:0] INPUT_BallX_8b,
  input  res,
  input  [7:0] INPUT_BallY_8b,
  input  run,
  output [7:0] out_7
);

  wire and_1_out, and_2_out, and_3_out, and_4_out, and_5_out, and_6_out, block_t, cdm_8_mark5_1_p1,
       cdm_8_mark5_1_p2, cdm_8_mark5_1_p4, cdm_8_mark5_1_p5, cdm_8_mark5_1_p6, cdm_8_mark5_1_p7,
       cdm_8_mark5_1_p8, clock, code, data, decoder_1_out0, decoder_1_out1, decoder_1_out3, decoder_1_out4,
       decoder_1_out5, decoder_1_out8, I_Osel, in_out_prime, mem, nand_1_out, nor_1_out, not_1_out,
       not_2_out, not_3_out, not_4_out, not_5_out, not_6_out, RAM;
  wire [3:0] I_Oadr;
  wire [7:0] cdm_8_mark5_1_p12, cdm_8_mark5_1_p13, divider_1_out, I_Odat, register_1_q, register_2_q;
  wire [7:4] cdm_8_mark5_1_p11;

  Decoder #(.select(4), .enable("false")) decoder_1 (
    .out0(decoder_1_out0), .out1(decoder_1_out1), .out3(decoder_1_out3), .out4(decoder_1_out4),
    .out5(decoder_1_out5), .out8(decoder_1_out8), .sel(I_Oadr));  // open: out2, out6, out7, out9, out10, out11, out12, out13, out14, out15
  and and_1 (and_1_out, decoder_1_out0, I_Osel, ~in_out_prime);  // AND_Gate
  and and_2 (and_2_out, decoder_1_out1, in_out_prime, I_Osel);
  Register #(.trigger("high")) register_1 (.D(I_Odat), .Q(register_1_q), .clk(and_1_out));  // open: en, clr
  Divider divider_1 (.a(register_1_q), .b(8'h3), .out(divider_1_out));  // open: upper, rem
  assign I_Odat = and_2_out ? divider_1_out : 8'bz;  // Controlled_Buffer controlled_buffer_1
  not not_1 (not_1_out, in_out_prime);
  LED led_1 (.in(and_3_out));
  and and_3 (and_3_out, not_1_out, I_Osel, decoder_1_out8);
  LED led_2 (.in(and_3_out));
  and and_4 (and_4_out, in_out_prime, I_Osel, decoder_1_out3);
  LED led_3 (.in(and_4_out));
  LED led_4 (.in(and_5_out));
  and and_5 (and_5_out, in_out_prime, I_Osel, decoder_1_out4);
  and and_6 (and_6_out, in_out_prime, I_Osel, decoder_1_out5);
  LED led_5 (.in(and_6_out));
  assign I_Odat = and_4_out ? register_2_q : 8'bz;  // Controlled_Buffer controlled_buffer_2
  assign I_Odat = and_5_out ? INPUT_BallX_8b : 8'bz;  // Controlled_Buffer controlled_buffer_3
  assign I_Odat = and_6_out ? INPUT_BallY_8b : 8'bz;  // Controlled_Buffer controlled_buffer_4
  nor nor_1 (nor_1_out, and_2_out, and_1_out, and_3_out, and_4_out, and_5_out, and_6_out);
  not not_2 (not_2_out, block_t);
  Register register_2 (.D(in_1), .en(not_3_out), .Q(register_2_q), .clk(clock), .clr(block_t));
  not not_3 (not_3_out, block_t);
  and and_7 (RAM, nor_1_out, data);
  Register register_3 (.D(I_Odat), .en(not_2_out), .Q(out_7), .clk(and_3_out));  // open: clr
  // Probe on I_Oadr
  // Probe on I_Odat
  Clock clock_1 (.out(clock));
  and and_8 (I_Osel, not_4_out, clock, data);
  or or_1 (block_t, block, res, run);
  // Probe on nothing
  // Probe on cdm_8_mark5_1_p5
  // Probe on cdm_8_mark5_1_p4
  // Probe on cdm_8_mark5_1_p2
  // Probe on cdm_8_mark5_1_p1
  not not_4 (not_4_out, nand_1_out);
  // Probe on cdm_8_mark5_1_p6
  // Probe on cdm_8_mark5_1_p7
  // CdM_8_mark5 cdm_8_mark5_1: pin names not known; wires that end beside it: cdm_8_mark5_1_p1, cdm_8_mark5_1_p2, clock, cdm_8_mark5_1_p4, cdm_8_mark5_1_p5, cdm_8_mark5_1_p6, cdm_8_mark5_1_p7, cdm_8_mark5_1_p8, mem, in_out_prime, {cdm_8_mark5_1_p11, I_Oadr}, cdm_8_mark5_1_p12, cdm_8_mark5_1_p13
  nand nand_1 (nand_1_out, cdm_8_mark5_1_p11[4], cdm_8_mark5_1_p11[5], cdm_8_mark5_1_p11[6], cdm_8_mark5_1_p11[7]);
  Decoder #(.disabled(0)) decoder_2 (.out0(code), .out1(data), .sel(cdm_8_mark5_1_p8), .en(mem));
  assign I_Odat = not_5_out ? cdm_8_mark5_1_p12 : 8'bz;  // Controlled_Buffer controlled_buffer_5
  not not_5 (not_5_out, in_out_prime);
  assign cdm_8_mark5_1_p13 = in_out_prime ? I_Odat : 8'bz;  // Controlled_Buffer controlled_buffer_6
  not not_6 (not_6_out, in_out_prime);
  Pull_Resistor pull_resistor_1 (.node(I_Oadr[0]));
  Pull_Resistor pull_resistor_2 (.node(I_Oadr[1]));
  Pull_Resistor pull_resistor_3 (.node(I_Oadr[2]));
  Pull_Resistor pull_resistor_4 (.node(I_Oadr[3]));
  Pull_Resistor pull_resistor_5 (.node(cdm_8_mark5_1_p11[4]));
  Pull_Resistor pull_resistor_6 (.node(cdm_8_mark5_1_p11[5]));
  Pull_Resistor pull_resistor_7 (.node(cdm_8_mark5_1_p11[6]));
  Pull_Resistor pull_resistor_8 (.node(cdm_8_mark5_1_p11[7]));
  ROM rom_1 (.addr({cdm_8_mark5_1_p11, I_Oadr}), .data(I_Odat), .sel(code));
  RAM #(.bus("separate")) ram_1 (
    .addr({cdm_8_mark5_1_p11, I_Oadr}), .din(I_Odat), .data(I_Odat), .str(not_6_out), .sel(RAM), .clk(clock),
    .ld(in_out_prime), .clr(res));

  // Other names for the same wires on the sheet: rd_wr_prime = in_out_prime; resey = res

  // Notes on the sheet:
  //   0xf0
  //   0xf1
  //   (because proramm can't divide fast)
  //   in case vx = | 3 |
  //   IO 0xf8
  //   IO 0xf3
  //   IO 0xf4
  //   IO 0xf5
  //   OUTPUT 0xf8 addr
  //   INPUT Vxy (0b00yyyxxx)
  //   RightBat Y
  //   *to controller
  //   I/O BUS
  //   4 lower bit adr
  //   "robot_release.asm"
  //   INSTR
  //   contents of rom_1 (hex, n*v repeats v):
  //   d0 f3 b0 d2 f5 ba d1 f4 b5 0 e1 11 d0 f8 a2 ee 0 d3 4 43 f ed 1c d0 f8 a2 ee 0 85 d3 e4 1d c0 d3 7
  //   4c 84 d3 fd 7c e1 32 d0 f0 a1 d1 f1 b5 ee 3b d3 fe 7c e1 3b 91 d3 7f 4d c4 d3 20 73 ea 7f 98 98 98
  //   d3 3 73 e1 5c d0 ff a2 6 d0 0 d3 0 15 23 d0 0 19 23 d0 ff b2 ee 6b d3 2 73 e1 69 d3 0 d0 0 15 23 ee
  //   6b d3 0 d0 0 16 23 d0 1 43 f e1 77 ee 78 86 d0 f8 a2 ee 0 ee c1 98 98 98 d3 f8 5c d3 fd 73 e1 9e d0
  //   ff a2 6 d3 0 d0 0 19 23 d0 0 19 23 d0 ff b2 85 ee af d3 fe 73 e1 ac d3 0 d0 0 15 23 85 ee af d3 0 85
  //   d0 0 16 23 d0 1 43 f e1 bc 86 ee bc d0 f8 a2 ee 0 d4
  //   DATA
endmodule

module switch (
  input  tap_here_x2,
  output out_2
);

  Counter #(.width(1), .max('h1)) counter_1 (
    .D(tap_here_x2), .Q(out_2), .clk(tap_here_x2));  // open: load, count, carry, clr

  // Notes on the sheet:
  //   ^
  //   |
  //   and again
endmodule

module Level (
  input  res,
  input  set,
  input  [4:0] in_3,
  output no_start,
  output hard,
  output norm,
  output ez
);

  wire clock_1_out, not_1_out;
  wire [4:0] register_2_q;

  Register #(.width(1), .trigger("high")) register_1 (.D(1'b1), .Q(no_start), .clk(set), .clr(res));  // open: en
  not not_1 (not_1_out, no_start);
  Register #(.width(5), .trigger("high")) register_2 (
    .D(in_3), .en(not_1_out), .Q(register_2_q), .clk(clock_1_out));  // open: clr
  Clock clock_1 (.out(clock_1_out));
  Comparator #(.width(5), .mode("unsigned")) comparator_1 (.a(register_2_q), .b(5'b10100), .gt(hard));  // open: eq, lt
  Comparator #(.width(5), .mode("unsigned")) comparator_2 (.a(register_2_q), .b(5'b01001), .lt(ez));  // open: gt, eq
  nor nor_1 (norm, hard, ez);

  // Notes on the sheet:
  //   aka menu
endmodule

module Joystick (
  input  [4:0] in_1,
  output [4:0] out_2
);

  wire and_1_out, and_2_out, clock_1_out, comparator_1_eq, comparator_2_gt, comparator_3_lt, not_1_out,
       not_2_out, not_3_out;
  wire [4:0] register_2_q;

  Clock clock_1 (.out(clock_1_out));
  Register #(.width(5)) register_1 (.D(in_1), .en(not_2_out), .Q(out_2), .clk(clock_1_out));  // open: clr
  not not_1 (not_1_out, clock_1_out);
  not not_2 (not_2_out, and_2_out);
  Register #(.width(5)) register_2 (.D(out_2), .Q(register_2_q), .clk(not_1_out));  // open: en, clr
  Comparator #(.width(5), .mode("unsigned")) comparator_1 (
    .a(in_1), .b(5'b10000), .eq(comparator_1_eq));  // open: gt, lt
  Comparator #(.width(5), .mode("unsigned")) comparator_2 (
    .a(register_2_q), .b(5'b01101), .gt(comparator_2_gt));  // open: eq, lt
  Comparator #(.width(5), .mode("unsigned")) comparator_3 (
    .a(register_2_q), .b(5'b10011), .lt(comparator_3_lt));  // open: gt, eq
  and and_1 (and_1_out, comparator_2_gt, comparator_3_lt);
  and and_2 (and_2_out, comparator_1_eq, not_3_out);
  not not_3 (not_3_out, and_1_out);

  // Notes on the sheet:
  //   This circuit fixates left bat when player suddenly lets go the joysyick
endmodule

module Menu_graphics (
  input  [4:0] chip_id,
  input  [2:0] level,
  output [31:0] out_3
);

  wire and_1_out, and_2_out, and_3_out, and_4_out, and_5_out, and_6_out, and_7_out, decoder_1_out3,
       decoder_1_out4, decoder_1_out5, decoder_1_out6, decoder_1_out7, decoder_1_out8, decoder_1_out9,
       decoder_1_out10, decoder_1_out11, decoder_1_out12, decoder_1_out13, decoder_1_out14, decoder_1_out15,
       decoder_1_out16, decoder_1_out18, decoder_1_out19, decoder_1_out20, decoder_1_out21, decoder_1_out22,
       mark;
  wire [31:0] controlled_buffer_1_out, controlled_buffer_21_out;

  Decoder #(.select(5), .enable("false")) decoder_1 (
    .out1(mark), .out3(decoder_1_out3), .out4(decoder_1_out4), .out5(decoder_1_out5), .out6(decoder_1_out6),
    .out7(decoder_1_out7), .out8(decoder_1_out8), .out9(decoder_1_out9), .out10(decoder_1_out10),
    .out11(decoder_1_out11), .out12(decoder_1_out12), .out13(decoder_1_out13), .out14(decoder_1_out14),
    .out15(decoder_1_out15), .out16(decoder_1_out16), .out18(decoder_1_out18), .out19(decoder_1_out19),
    .out20(decoder_1_out20), .out21(decoder_1_out21), .out22(decoder_1_out22), .sel(chip_id));  // open: out0, out2, out17, out23, out24, out25, out26, out27, out28, out29, out30, out31
  and and_1 (and_1_out, ~decoder_1_out3, ~decoder_1_out4, ~decoder_1_out5, ~decoder_1_out6, ~decoder_1_out7, ~decoder_1_out8);  // AND_Gate
  assign controlled_buffer_1_out = decoder_1_out7 ? {32{1'b0}} : 32'bz;  // Controlled_Buffer controlled_buffer_1
  assign controlled_buffer_1_out = decoder_1_out6 ? 32'hfbea800 : 32'bz;  // Controlled_Buffer controlled_buffer_2
  assign controlled_buffer_1_out = decoder_1_out5 ? 32'h208a800 : 32'bz;  // Controlled_Buffer controlled_buffer_3
  assign controlled_buffer_1_out = decoder_1_out4 ? 32'h210a800 : 32'bz;  // Controlled_Buffer controlled_buffer_4
  assign controlled_buffer_1_out = decoder_1_out3 ? 32'hfbef800 : 32'bz;  // Controlled_Buffer controlled_buffer_5
  assign controlled_buffer_1_out = decoder_1_out15 ? 32'ha28a800 : 32'bz;  // Controlled_Buffer controlled_buffer_6
  assign controlled_buffer_1_out = decoder_1_out14 ? 32'ha28a800 : 32'bz;  // Controlled_Buffer controlled_buffer_7
  assign controlled_buffer_1_out = decoder_1_out13 ? 32'hfbee800 : 32'bz;  // Controlled_Buffer controlled_buffer_8
  assign controlled_buffer_1_out = decoder_1_out12 ? {32{1'b0}} : 32'bz;  // Controlled_Buffer controlled_buffer_9
  assign controlled_buffer_1_out = decoder_1_out11 ? 32'h7be7800 : 32'bz;  // Controlled_Buffer controlled_buffer_10
  assign controlled_buffer_1_out = decoder_1_out10 ? 32'ha22a000 : 32'bz;  // Controlled_Buffer controlled_buffer_11
  assign controlled_buffer_1_out = decoder_1_out9 ? 32'ha22a000 : 32'bz;  // Controlled_Buffer controlled_buffer_12
  assign controlled_buffer_1_out = decoder_1_out8 ? 32'h7be7800 : 32'bz;  // Controlled_Buffer controlled_buffer_13
  assign controlled_buffer_1_out = decoder_1_out22 ? 32'h3e0000 : 32'bz;  // Controlled_Buffer controlled_buffer_14
  assign controlled_buffer_1_out = decoder_1_out21 ? 32'h7100000 : 32'bz;  // Controlled_Buffer controlled_buffer_15
  assign controlled_buffer_1_out = decoder_1_out20 ? 32'h888f800 : 32'bz;  // Controlled_Buffer controlled_buffer_16
  assign controlled_buffer_1_out = decoder_1_out19 ? 32'h8902800 : 32'bz;  // Controlled_Buffer controlled_buffer_17
  assign controlled_buffer_1_out = decoder_1_out18 ? 32'hfbee800 : 32'bz;  // Controlled_Buffer controlled_buffer_18
  assign controlled_buffer_1_out = decoder_1_out16 ? 32'hdb6b800 : 32'bz;  // Controlled_Buffer controlled_buffer_19
  and and_2 (and_2_out, ~decoder_1_out9, ~decoder_1_out10, ~decoder_1_out11, ~decoder_1_out12, ~decoder_1_out13, ~decoder_1_out14, ~decoder_1_out15, ~decoder_1_out16, ~decoder_1_out18, ~decoder_1_out19, ~decoder_1_out20, ~decoder_1_out21, ~decoder_1_out22);  // AND_Gate
  and and_3 (and_3_out, and_1_out, and_2_out);
  assign controlled_buffer_1_out = and_3_out ? {32{1'b0}} : 32'bz;  // Controlled_Buffer controlled_buffer_20
  and and_4 (and_4_out, mark, level[0]);
  assign controlled_buffer_21_out = and_4_out ? 32'h1000000 : 32'bz;  // Controlled_Buffer controlled_buffer_21
  and and_5 (and_5_out, level[1], mark);
  assign controlled_buffer_21_out = and_5_out ? 32'h80000 : 32'bz;  // Controlled_Buffer controlled_buffer_22
  and and_6 (and_6_out, level[2], mark);
  assign out_3 = controlled_buffer_1_out | controlled_buffer_21_out;  // OR_Gate or_1, 32 bits wide
  assign controlled_buffer_21_out = and_7_out ? {32{1'b0}} : 32'bz;  // Controlled_Buffer controlled_buffer_23
  and and_7 (and_7_out, ~and_4_out, ~and_5_out, ~and_6_out);  // AND_Gate
  assign controlled_buffer_21_out = and_6_out ? 32'h2000 : 32'bz;  // Controlled_Buffer controlled_buffer_24

  // Other names for the same wires on the sheet: level_mark[2:0] = level
endmodule

module Difficulty_mechanics (
  input  [7:0] ball_X,
  input  [2:0] level,
  input  [7:0] right_bat,
  input  [7:0] VX,
  output [2:0] VY,
  output [2:0] VX_2,
  output [7:0] right_bat_fin
);

  wire and_1_out, and_2_out, and_3_out, and_4_out, and_5_out, clock_1_out, comparator_1_gt, comparator_2_lt,
       comparator_3_lt, comparator_4_gt, decoder_1_out0, decoder_1_out1, decoder_1_out2, decoder_1_out3,
       decoder_1_out4, decoder_1_out5, decoder_1_out6, decoder_1_out7, decoder_1_out8, decoder_1_out9, miss,
       not_1_out, or_1_out, or_2_out, or_3_out, or_4_out, P, reset, sign, \time ;
  wire [2:0] controlled_inverter_1_out;
  wire [3:0] random_1_out;
  wire [4:0] divider_1_rem;
  wire [7:0] adder_2_out, multiplexer_1_out;

  assign VY = level[0] ? 3'b011 : 3'bz;  // Controlled_Buffer controlled_buffer_1
  Comparator #(.mode("unsigned")) comparator_1 (.a(right_bat), .b(8'h12), .gt(comparator_1_gt));  // open: eq, lt
  Comparator #(.mode("unsigned")) comparator_2 (.a(right_bat), .b(8'hef), .lt(comparator_2_lt));  // open: gt, eq
  // Probe on ball_X
  assign VY = level[1] ? 3'b010 : 3'bz;  // Controlled_Buffer controlled_buffer_2
  assign VY = level[2] ? 3'b001 : 3'bz;  // Controlled_Buffer controlled_buffer_3
  assign controlled_inverter_1_out = level[1] ? ~VY : 3'bz;  // Controlled_Inverter controlled_inverter_1
  assign controlled_inverter_1_out = level[2] ? ~3'b011 : 3'bz;  // Controlled_Inverter controlled_inverter_2
  and and_1 (and_1_out, comparator_1_gt, sign);
  and and_2 (and_2_out, ~sign, ~comparator_2_lt);  // AND_Gate
  Comparator #(.mode("unsigned")) comparator_3 (.a(ball_X), .b(8'h50), .gt(P), .lt(comparator_3_lt));  // open: eq
  or or_1 (or_1_out, comparator_3_lt, comparator_4_gt);
  Comparator #(.mode("unsigned")) comparator_4 (.a(ball_X), .b(8'h9f), .gt(comparator_4_gt));  // open: eq, lt
  nor nor_1 (reset, level[2], level[1], level[0]);
  assign VY = reset ? 3'b000 : 3'bz;  // Controlled_Buffer controlled_buffer_4
  assign controlled_inverter_1_out = level[0] ? ~3'b001 : 3'bz;  // Controlled_Inverter controlled_inverter_3
  Adder #(.width(3)) adder_1 (.a(controlled_inverter_1_out), .b(3'b001), .out(VX_2));  // open: cin, cout
  Clock clock_1 (.out(clock_1_out));
  not not_1 (not_1_out, or_1_out);
  assign VX_2 = reset ? 3'b000 : 3'bz;  // Controlled_Buffer controlled_buffer_5
  or or_2 (or_2_out, and_1_out, and_2_out);
  S_R_Flip_Flop s_r_ff_1 (.S(not_1_out), .clk(clock_1_out), .R(or_1_out), .Q(\time ));  // open: Qn, preset, reset, en
  // Probe on {sign, random_1_out}
  Random #(.width(5), .seed(833264259)) random_1 (.clk(P), .out({sign, random_1_out}));  // open: next, clr
  Divider #(.width(5)) divider_1 (.a({sign, random_1_out}), .b(5'b01010), .rem(divider_1_rem));  // open: out, upper
  Multiplexer #(.width(8), .enable("false")) multiplexer_1 (
    .in0(8'h16), .in1(8'hf0), .out(multiplexer_1_out), .sel(or_2_out));
  // Probe on right_bat
  Decoder #(.select(5), .enable("false")) decoder_1 (
    .out0(decoder_1_out0), .out1(decoder_1_out1), .out2(decoder_1_out2), .out3(decoder_1_out3),
    .out4(decoder_1_out4), .out5(decoder_1_out5), .out6(decoder_1_out6), .out7(decoder_1_out7),
    .out8(decoder_1_out8), .out9(decoder_1_out9), .sel(divider_1_rem));  // open: out10, out11, out12, out13, out14, out15, out16, out17, out18, out19, out20, out21, out22, out23, out24, out25, out26, out27, out28, out29, out30, out31
  Adder adder_2 (.a(multiplexer_1_out), .b(right_bat), .out(adder_2_out));  // open: cin, cout
  or or_3 (or_3_out, decoder_1_out2, decoder_1_out8, decoder_1_out9, decoder_1_out6);
  or or_4 (or_4_out, decoder_1_out1, decoder_1_out7);
  Multiplexer #(.width(8), .enable("false")) multiplexer_2 (
    .in0(right_bat), .in1(adder_2_out), .out(right_bat_fin), .sel(and_3_out));
  and and_3 (and_3_out, ~VX[2], miss, \time );  // AND_Gate
  and and_4 (and_4_out, or_3_out, level[2]);
  and and_5 (and_5_out, level[1], or_4_out);
  // Probe on right_bat_fin
  or or_5 (miss, and_4_out, and_5_out);

  // Other names for the same wires on the sheet: hard = level[0]; normal = level[1]; easy = level[2]

  // Notes on the sheet:
  //   hard -> vx|vy = 1|3 missing P = 0
  //   normal -> vx|vy = 2|2 missing P in time ~ 2/10
  //   easy -> vx|vy = 3|1 missing P in time ~ 4/10
  //   when ball goes left -> no misses
  //   9
  //   random() % 10
  //   switch bat with -16/16
  //   right bat to miss
endmodule

module Game_over_graphics (
  input  [4:0] chip_id,
  input  [1:0] game_resault,
  output [31:0] out_3
);

  wire decoder_1_out8, decoder_1_out9, decoder_1_out10, decoder_1_out11, decoder_1_out12, decoder_1_out13,
       decoder_1_out14, decoder_1_out15, decoder_1_out16, decoder_1_out17, decoder_1_out18, decoder_1_out19,
       decoder_1_out20, decoder_1_out21, decoder_1_out22, decoder_1_out23, decoder_2_out0, decoder_2_out1,
       decoder_2_out2, decoder_2_out3, decoder_2_out4, decoder_2_out5, decoder_2_out6, decoder_2_out7,
       decoder_2_out8, decoder_2_out9, decoder_2_out10, decoder_2_out11, decoder_2_out12, decoder_2_out13,
       decoder_2_out14, decoder_2_out15, decoder_2_out16, decoder_2_out17, decoder_2_out18, decoder_2_out19,
       decoder_2_out20, decoder_2_out21, decoder_2_out22, decoder_2_out23, decoder_2_out24, decoder_2_out25,
       decoder_2_out26, decoder_2_out27, decoder_2_out28, decoder_2_out29, decoder_2_out30, decoder_2_out31,
       nor_1_out, or_1_out;
  wire [31:0] controlled_buffer_1_out, controlled_buffer_2_out, multiplexer_1_out, not_1_out;

  Decoder #(.select(5), .enable("false")) decoder_1 (
    .out8(decoder_1_out8), .out9(decoder_1_out9), .out10(decoder_1_out10), .out11(decoder_1_out11),
    .out12(decoder_1_out12), .out13(decoder_1_out13), .out14(decoder_1_out14), .out15(decoder_1_out15),
    .out16(decoder_1_out16), .out17(decoder_1_out17), .out18(decoder_1_out18), .out19(decoder_1_out19),
    .out20(decoder_1_out20), .out21(decoder_1_out21), .out22(decoder_1_out22), .out23(decoder_1_out23),
    .sel(chip_id));  // open: out0, out1, out2, out3, out4, out5, out6, out7, out24, out25, out26, out27, out28, out29, out30, out31
  assign controlled_buffer_1_out = decoder_1_out8 ? 32'he000 : 32'bz;  // Controlled_Buffer controlled_buffer_1
  Decoder #(.select(5), .enable("false")) decoder_2 (
    .out0(decoder_2_out0), .out1(decoder_2_out1), .out2(decoder_2_out2), .out3(decoder_2_out3),
    .out4(decoder_2_out4), .out5(decoder_2_out5), .out6(decoder_2_out6), .out7(decoder_2_out7),
    .out8(decoder_2_out8), .out9(decoder_2_out9), .out10(decoder_2_out10), .out11(decoder_2_out11),
    .out12(decoder_2_out12), .out13(decoder_2_out13), .out14(decoder_2_out14), .out15(decoder_2_out15),
    .out16(decoder_2_out16), .out17(decoder_2_out17), .out18(decoder_2_out18), .out19(decoder_2_out19),
    .out20(decoder_2_out20), .out21(decoder_2_out21), .out22(decoder_2_out22), .out23(decoder_2_out23),
    .out24(decoder_2_out24), .out25(decoder_2_out25), .out26(decoder_2_out26), .out27(decoder_2_out27),
    .out28(decoder_2_out28), .out29(decoder_2_out29), .out30(decoder_2_out30), .out31(decoder_2_out31),
    .sel(chip_id));
  assign controlled_buffer_2_out = decoder_2_out4 ? 32'h70000 : 32'bz;  // Controlled_Buffer controlled_buffer_2
  assign controlled_buffer_2_out = decoder_2_out3 ? 32'hc000 : 32'bz;  // Controlled_Buffer controlled_buffer_3
  assign controlled_buffer_2_out = decoder_2_out2 ? 32'h70000 : 32'bz;  // Controlled_Buffer controlled_buffer_4
  assign controlled_buffer_1_out = decoder_1_out16 ? 32'h1e8800 : 32'bz;  // Controlled_Buffer controlled_buffer_5
  assign controlled_buffer_1_out = decoder_1_out15 ? 32'h12f800 : 32'bz;  // Controlled_Buffer controlled_buffer_6
  assign controlled_buffer_1_out = decoder_1_out14 ? 32'h1e8800 : 32'bz;  // Controlled_Buffer controlled_buffer_7
  assign controlled_buffer_1_out = decoder_1_out13 ? {32{1'b0}} : 32'bz;  // Controlled_Buffer controlled_buffer_8
  assign controlled_buffer_1_out = decoder_1_out12 ? 32'h1ee000 : 32'bz;  // Controlled_Buffer controlled_buffer_9
  assign controlled_buffer_1_out = decoder_1_out11 ? 32'ha1800 : 32'bz;  // Controlled_Buffer controlled_buffer_10
  assign controlled_buffer_1_out = decoder_1_out10 ? 32'h1ae000 : 32'bz;  // Controlled_Buffer controlled_buffer_11
  assign controlled_buffer_1_out = decoder_1_out9 ? 32'h1800 : 32'bz;  // Controlled_Buffer controlled_buffer_12
  assign controlled_buffer_2_out = decoder_2_out12 ? {32{1'b0}} : 32'bz;  // Controlled_Buffer controlled_buffer_13
  assign controlled_buffer_2_out = decoder_2_out11 ? 32'h3c000 : 32'bz;  // Controlled_Buffer controlled_buffer_14
  assign controlled_buffer_2_out = decoder_2_out10 ? 32'h50000 : 32'bz;  // Controlled_Buffer controlled_buffer_15
  assign controlled_buffer_2_out = decoder_2_out9 ? 32'h50000 : 32'bz;  // Controlled_Buffer controlled_buffer_16
  assign controlled_buffer_2_out = decoder_2_out8 ? 32'h3c000 : 32'bz;  // Controlled_Buffer controlled_buffer_17
  assign controlled_buffer_2_out = decoder_2_out7 ? {32{1'b0}} : 32'bz;  // Controlled_Buffer controlled_buffer_18
  assign controlled_buffer_2_out = decoder_2_out6 ? 32'h70000 : 32'bz;  // Controlled_Buffer controlled_buffer_19
  assign controlled_buffer_2_out = decoder_2_out5 ? 32'hc000 : 32'bz;  // Controlled_Buffer controlled_buffer_20
  assign controlled_buffer_1_out = decoder_1_out23 ? 32'h3e800 : 32'bz;  // Controlled_Buffer controlled_buffer_21
  assign controlled_buffer_1_out = decoder_1_out22 ? {32{1'b0}} : 32'bz;  // Controlled_Buffer controlled_buffer_22
  assign controlled_buffer_1_out = decoder_1_out21 ? 32'h1ef800 : 32'bz;  // Controlled_Buffer controlled_buffer_23
  assign controlled_buffer_1_out = decoder_1_out20 ? 32'h21000 : 32'bz;  // Controlled_Buffer controlled_buffer_24
  assign controlled_buffer_1_out = decoder_1_out19 ? 32'h22000 : 32'bz;  // Controlled_Buffer controlled_buffer_25
  assign controlled_buffer_1_out = decoder_1_out18 ? 32'h1ef800 : 32'bz;  // Controlled_Buffer controlled_buffer_26
  assign controlled_buffer_1_out = decoder_1_out17 ? {32{1'b0}} : 32'bz;  // Controlled_Buffer controlled_buffer_27
  assign controlled_buffer_2_out = decoder_2_out20 ? 32'h40000 : 32'bz;  // Controlled_Buffer controlled_buffer_28
  assign controlled_buffer_2_out = decoder_2_out19 ? 32'h7c000 : 32'bz;  // Controlled_Buffer controlled_buffer_29
  assign controlled_buffer_2_out = decoder_2_out18 ? 32'h40000 : 32'bz;  // Controlled_Buffer controlled_buffer_30
  assign controlled_buffer_2_out = decoder_2_out17 ? {32{1'b0}} : 32'bz;  // Controlled_Buffer controlled_buffer_31
  assign controlled_buffer_2_out = decoder_2_out16 ? 32'h5c000 : 32'bz;  // Controlled_Buffer controlled_buffer_32
  assign controlled_buffer_2_out = decoder_2_out15 ? 32'h54000 : 32'bz;  // Controlled_Buffer controlled_buffer_33
  assign controlled_buffer_2_out = decoder_2_out14 ? 32'h54000 : 32'bz;  // Controlled_Buffer controlled_buffer_34
  assign controlled_buffer_2_out = decoder_2_out13 ? 32'h74000 : 32'bz;  // Controlled_Buffer controlled_buffer_35
  assign controlled_buffer_2_out = decoder_2_out28 ? 32'h44000 : 32'bz;  // Controlled_Buffer controlled_buffer_36
  assign controlled_buffer_2_out = decoder_2_out27 ? 32'h44000 : 32'bz;  // Controlled_Buffer controlled_buffer_37
  assign controlled_buffer_2_out = decoder_2_out26 ? 32'h7c000 : 32'bz;  // Controlled_Buffer controlled_buffer_38
  assign controlled_buffer_2_out = decoder_2_out25 ? {32{1'b0}} : 32'bz;  // Controlled_Buffer controlled_buffer_39
  assign controlled_buffer_2_out = decoder_2_out24 ? 32'h54000 : 32'bz;  // Controlled_Buffer controlled_buffer_40
  assign controlled_buffer_2_out = decoder_2_out23 ? 32'h54000 : 32'bz;  // Controlled_Buffer controlled_buffer_41
  assign controlled_buffer_2_out = decoder_2_out22 ? 32'h7c000 : 32'bz;  // Controlled_Buffer controlled_buffer_42
  assign controlled_buffer_2_out = decoder_2_out21 ? {32{1'b0}} : 32'bz;  // Controlled_Buffer controlled_buffer_43
  nor nor_1 (nor_1_out, decoder_1_out8, decoder_1_out9, decoder_1_out10, decoder_1_out11, decoder_1_out12, decoder_1_out13, decoder_1_out14, decoder_1_out15, decoder_1_out16, decoder_1_out17, decoder_1_out18, decoder_1_out19, decoder_1_out20, decoder_1_out21, decoder_1_out22, decoder_1_out23);
  or or_1 (or_1_out, decoder_2_out31, decoder_2_out30, decoder_2_out1, decoder_2_out0);
  assign controlled_buffer_2_out = decoder_2_out29 ? 32'h38000 : 32'bz;  // Controlled_Buffer controlled_buffer_44
  assign not_1_out = ~controlled_buffer_2_out;  // NOT_Gate not_1, 32 bits wide
  assign controlled_buffer_2_out = or_1_out ? {32{1'b0}} : 32'bz;  // Controlled_Buffer controlled_buffer_45
  Multiplexer #(.width(32), .enable("false")) multiplexer_1 (
    .in0(controlled_buffer_1_out), .in1({32{1'b0}}), .out(multiplexer_1_out), .sel(nor_1_out));
  DotMatrix #(.matrixcols(32), .matrixrows(32)) dotmatrix_1 (
    .col2(32'h70000), .col3(32'hc000), .col4(32'h70000), .col5(32'hc000), .col6(32'h70000),
    .col7({32{1'b0}}), .col8(32'h3c000), .col9(32'h50000), .col10(32'h50000), .col11(32'h3c000),
    .col12({32{1'b0}}), .col13(32'h74000), .col14(32'h54000), .col15(32'h54000), .col16(32'h5c000),
    .col17({32{1'b0}}), .col18(32'h40000), .col19(32'h7c000), .col20(32'h40000), .col21({32{1'b0}}),
    .col22(32'h7c000), .col23(32'h54000), .col24(32'h54000), .col25({32{1'b0}}), .col26(32'h7c000),
    .col27(32'h44000), .col28(32'h44000), .col29(32'h38000));  // open: col0, col1, col30, col31
  Multiplexer #(.select(2), .width(32), .enable("false")) multiplexer_2 (
    .in1(multiplexer_1_out), .in2(not_1_out), .out(out_3), .sel(game_resault));  // open: in0, in3

  // Other names for the same wires on the sheet: res[1:0] = game_resault

  // Notes on the sheet:
  //   you win !
  //   wasted
endmodule
